// Logisim project ALU.circ as structural Verilog: 4 circuits, main circuit ALU
module ALU (
  input  [31:0] A,
  input  [31:0] B,
  input  [3:0] ALU_Control,
  output [31:0] Result,
  output Zero_Flag,
  output Negative_Flag,
  output [31:0] Hi
);

  wire comparator_1_lt, comparator_2_lt, comparator_3_eq, comparator_4_eq, comparator_5_eq;
  wire [31:0] Add, And, Nor, Or, or_2_out, SDivHi, SDivLo, Slt, Sltu, SMulHi, SMulLo, Sub, UDivHi, UDivLo,
       UMulHi, UMulLo, Xor;

  Adder #(.width(32)) adder_1 (.a(A), .b(B), .out(Add));  // open: cin, cout
  Subtractor #(.width(32)) subtractor_1 (.a(A), .b(B), .out(Sub));  // open: bin, bout
  assign And = A & B;  // AND_Gate and_1, 32 bits wide
  assign Or = A | B;  // OR_Gate or_1, 32 bits wide
  assign Nor = ~or_2_out;  // NOT_Gate not_1, 32 bits wide
  assign or_2_out = A | B;  // OR_Gate or_2, 32 bits wide
  assign Xor = A ^ B;  // XOR_Gate xor_1, 32 bits wide
  Comparator #(.width(32)) comparator_1 (.a(A), .b(B), .lt(comparator_1_lt));  // open: gt, eq
  assign Slt = {{31{1'b0}}, comparator_1_lt};  // Bit_Extender bit_extender_1
  Comparator #(.width(32), .mode("unsigned")) comparator_2 (.a(A), .b(B), .lt(comparator_2_lt));  // open: gt, eq
  assign Sltu = {{31{1'b0}}, comparator_2_lt};  // Bit_Extender bit_extender_2
  Multiplier #(.width(32)) multiplier_1 (.a(A), .b(B), .out(SMulLo), .cout(SMulHi));  // open: cin
  Signed_Div signed_div_1 (.A(A), .B(B), .Lo(SDivHi), .Hi(SDivLo));
  Multiplexer #(.select(4), .width(32), .enable("false")) multiplexer_1 (
    .in0(Add), .in1(Sub), .in2(And), .in3(Or), .in4(Nor), .in5(Xor), .in6(Slt), .in7(Sltu), .in8(SMulLo),
    .in9(UMulLo), .in10(SDivLo), .in11(UDivLo), .in12({32{1'b0}}), .in13({32{1'b0}}), .in14({32{1'b0}}),
    .in15({32{1'b0}}), .out(Result), .sel(ALU_Control));
  Unsigned_Mult unsigned_mult_1 (.A(A), .B(B), .Hi(UMulHi), .Lo(UMulLo));
  Divider #(.width(32)) divider_1 (.a(A), .b(B), .out(UDivLo), .rem(UDivHi));  // open: upper
  Multiplexer #(.select(4), .width(32), .enable("false")) multiplexer_2 (
    .in0({32{1'b0}}), .in1({32{1'b0}}), .in2({32{1'b0}}), .in3({32{1'b0}}), .in4({32{1'b0}}),
    .in5({32{1'b0}}), .in6({32{1'b0}}), .in7({32{1'b0}}), .in8(SMulHi), .in9(UMulHi), .in10(SDivHi),
    .in11(UDivHi), .in12({32{1'b0}}), .in13({32{1'b0}}), .in14({32{1'b0}}), .in15({32{1'b0}}), .out(Hi),
    .sel(ALU_Control));
  Comparator #(.width(32)) comparator_3 (.a(Result), .b({32{1'b0}}), .eq(comparator_3_eq));  // open: gt, lt
  Comparator #(.width(32)) comparator_4 (.a(Hi), .b({32{1'b0}}), .eq(comparator_4_eq));  // open: gt, lt
  Multiplexer #(.enable("false")) multiplexer_3 (
    .in0(Result[31]), .in1(Hi[31]), .out(Negative_Flag), .sel(comparator_5_eq));
  Comparator #(.width(4), .mode("unsigned")) comparator_5 (
    .a(ALU_Control), .b(4'b1000), .eq(comparator_5_eq));  // open: gt, lt
  and and_2 (Zero_Flag, comparator_3_eq, comparator_4_eq);

  // Other names for the same wires on the sheet: crtl[3:0] = ALU_Control

  // Notes on the sheet:
  //   Input
  //   Addition
  //   Substraction
  //   Logical Ops
  //   Set Less Than
  //   Signed
  //   Unsigned
  //   Signed
  //   Signed
  //   Multiplication
  //   Result MUX
  //   Division
  //   Unsigned
  //   Unsigned
  //   Hi MUX
endmodule

module Unsigned_Mult (
  input  [31:0] A,
  input  [31:0] B,
  output [31:0] Hi,
  output [31:0] Lo
);

  wire adder_1_cout, adder_5_cout, and_1_out;
  wire [31:0] A_t, and_2_out, and_3_out, B_t, bit_extender_3_out, bit_extender_4_out, bit_extender_5_out,
       bit_extender_6_out, bit_extender_8_out, Hi1, Hi2, Hi3, Hi4, Hi5, Hi6, Hi7, Hi8, Hi9, Hi10, Lo1, Lo3,
       Lo4, Lo5;

  assign A_t = {{1{1'b0}}, A[30:0]};  // Bit_Extender bit_extender_1
  assign B_t = {{1{1'b0}}, B[30:0]};  // Bit_Extender bit_extender_2
  and and_1 (and_1_out, A[31], B[31]);
  Multiplier #(.width(32)) multiplier_1 (.a(A_t), .b(B_t), .out(Lo1), .cout(Hi1));  // open: cin
  assign bit_extender_3_out = {{31{1'b0}}, and_1_out};  // Bit_Extender bit_extender_3
  assign bit_extender_4_out = {{31{A[31]}}, A[31]};  // Bit_Extender bit_extender_4
  assign bit_extender_5_out = {{31{B[31]}}, B[31]};  // Bit_Extender bit_extender_5
  Shifter #(.width(32)) shifter_1 (.in(bit_extender_3_out), .\dist (5'b11110), .out(Hi2));
  assign and_2_out = bit_extender_4_out & B_t;  // AND_Gate and_2, 32 bits wide
  assign and_3_out = bit_extender_5_out & A_t;  // AND_Gate and_3, 32 bits wide
  assign bit_extender_6_out = {{31{1'b0}}, and_2_out[0]};  // Bit_Extender bit_extender_6
  assign Hi3 = {{1{1'b0}}, and_2_out[31:1]};  // Bit_Extender bit_extender_7
  assign bit_extender_8_out = {{31{1'b0}}, and_3_out[0]};  // Bit_Extender bit_extender_8
  assign Hi4 = {{1{1'b0}}, and_3_out[31:1]};  // Bit_Extender bit_extender_9
  Shifter #(.width(32)) shifter_2 (.in(bit_extender_6_out), .\dist ({5{1'b1}}), .out(Lo3));
  Shifter #(.width(32)) shifter_3 (.in(bit_extender_8_out), .\dist ({5{1'b1}}), .out(Lo4));
  Adder #(.width(32)) adder_1 (.a(Lo3), .b(Lo4), .out(Lo5), .cout(adder_1_cout));  // open: cin
  Adder #(.width(32)) adder_2 (.a(Hi3), .b(Hi4), .out(Hi6));  // open: cin, cout
  Adder #(.width(32)) adder_3 (.a(Hi2), .b(Hi6), .out(Hi7));  // open: cin, cout
  Adder #(.width(32)) adder_4 (.a(Hi1), .b(Hi7), .out(Hi8));  // open: cin, cout
  Adder #(.width(32)) adder_5 (.a(Lo1), .b(Lo5), .out(Lo), .cout(adder_5_cout));  // open: cin
  Adder #(.width(32)) adder_6 (.a(Hi8), .b(Hi9), .out(Hi10));  // open: cin, cout
  Adder #(.width(32)) adder_7 (.a(Hi10), .b(Hi5), .out(Hi));  // open: cin, cout
  assign Hi5 = {{31{1'b0}}, adder_1_cout};  // Bit_Extender bit_extender_10
  assign Hi9 = {{31{1'b0}}, adder_5_cout};  // Bit_Extender bit_extender_11

  // Other names for the same wires on the sheet: As = A[31]; Bs = B[31]
endmodule

module Signed_Div (
  input  [31:0] A,
  input  [31:0] B,
  output [31:0] Lo,
  output [31:0] Hi
);

  wire As, Bs, LoS;
  wire [31:0] Abs_A, Abs_B, Abs_Hi, Abs_Lo;

  Set_Sign set_sign_1 (.in_1(A), .cA(Abs_A), .Signo_A(As), .in_2(1'b0));
  Set_Sign set_sign_2 (.in_1(B), .cA(Abs_B), .Signo_A(Bs), .in_2(1'b0));
  Divider #(.width(32)) divider_1 (.a(Abs_A), .b(Abs_B), .out(Abs_Lo), .rem(Abs_Hi));  // open: upper
  xor xor_1 (LoS, As, Bs);
  Set_Sign set_sign_3 (.in_1(Abs_Lo), .cA(Lo), .in_2(LoS));  // open: Signo_A
  Set_Sign set_sign_4 (.in_1(Abs_Hi), .cA(Hi), .in_2(As));  // open: Signo_A

  // Other names for the same wires on the sheet: HiS = As
endmodule

module Set_Sign (
  input  [31:0] in_1,
  input  in_2,
  output [31:0] cA,
  output Signo_A
);

  wire [31:0] An, nA, pA;

  Negator #(.width(32)) negator_1 (.in(in_1), .out(An));
  Multiplexer #(.width(32), .disabled(0), .enable("false")) multiplexer_1 (
    .in0(in_1), .in1(An), .out(pA), .sel(in_1[31]));
  Negator #(.width(32)) negator_2 (.in(pA), .out(nA));
  Multiplexer #(.width(32), .disabled(0), .enable("false")) multiplexer_2 (.in0(pA), .in1(nA), .out(cA), .sel(in_2));

  assign Signo_A = in_1[31];

  // Other names for the same wires on the sheet: A[31:0] = in_1; As = in_1[31]; S = in_2
endmodule
