// Logisim project Caché.circ as structural Verilog: 8 circuits, main circuit Caché
module \Caché  (
  input  CS__Chip_Selector__when_1_the_cache_detectecs_a_R_W_command,
  input  R_W__0_to_read__1_to_write,
  input  [31:0] Address__Address_in_RAM_to_use,
  input  [31:0] Data__Data_to_Write,
  input  Clk,
  input  IorDS,
  input  Rst,
  input  Busy__Signal_of_RAM_in_use__When_Chache_asks_to_write_or_read_RAM_it_waits_for_this_to_become_0_once_it_finish,
  input  [31:0] Data_0,
  input  [31:0] Data_1,
  input  [31:0] Data_2,
  input  [31:0] Data_3,
  output Busy__Signals_that_RAM_is_in_use,
  output Hit__Signals_when_cache_had_the_required_value,
  output Miss__Signals_when_cache_didnt_have_the_required_value_and_needs_to_ask_RAM,
  output [31:0] Data__Data_output,
  output CS__Signals_when_cache_wants_RAM_to_R_W,
  output R_W__0_to_read_from_RAM__1_to_write_in_RAM,
  output [31:0] Address__Address_to_usee_in_RAM,
  output [31:0] Data_0_2,
  output [31:0] Data_1_2,
  output [31:0] Data_2_2,
  output [31:0] Data_3_2,
  output [3:0] Mask__Mask_to_signal_writing_rules_for_RAM
);

  wire BusyR_q, BusyW_q, comparator_1_eq, comparator_2_eq, decoder_2_out0, demultiplexer_1_out0,
       demultiplexer_1_out1, demultiplexer_2_out0, demultiplexer_3_out1, demultiplexer_4_out1, Dirty, Hit0,
       IDLE_q, Miss0, Miss1, multiplexer_6_out, not_5_out, or_4_out, or_8_out, or_10_out, Ram, Read, ReadD,
       SD, Val, Vd, Write, WriteD;
  wire [3:0] decoder_1_out0, MaskD, not_1_out;
  wire [9:0] TagOut;
  wire [31:0] D0, D0D, D1, D1D, D2, D2D, D3, D3D, multiplexer_1_out, or_3_out, register_1_q;

  Pull_Resistor pull_resistor_1 (.node(CS__Chip_Selector__when_1_the_cache_detectecs_a_R_W_command));
  Pull_Resistor pull_resistor_2 (.node(R_W__0_to_read__1_to_write));
  Pull_Resistor pull_resistor_3 (.node(Address__Address_in_RAM_to_use));
  Pull_Resistor pull_resistor_4 (.node(Data__Data_to_Write));
  Pull_Resistor pull_resistor_5 (.node(Busy__Signal_of_RAM_in_use__When_Chache_asks_to_write_or_read_RAM_it_waits_for_this_to_become_0_once_it_finish));
  Pull_Resistor pull_resistor_6 (.node(Data_0));
  Pull_Resistor pull_resistor_7 (.node(Data_1));
  Pull_Resistor pull_resistor_8 (.node(Data_2));
  Pull_Resistor pull_resistor_9 (.node(Data_3));
  Multiplexer #(.select(2), .width(32), .disabled(0)) multiplexer_1 (
    .in0(D0), .in1(D1), .in2(D2), .in3(D3), .out(multiplexer_1_out),
    .sel(Address__Address_in_RAM_to_use[3:2]), .en(ReadD));
  Register_part #(.width(32)) register_1 (.D(multiplexer_1_out), .en(1'b1), .Q(register_1_q), .clk(Clk), .clr(Rst));
  Pull_Resistor pull_resistor_10 (.node(Busy__Signals_that_RAM_is_in_use));
  or or_1 (Hit__Signals_when_cache_had_the_required_value, Hit0, WriteD);
  or or_2 (Miss__Signals_when_cache_didnt_have_the_required_value_and_needs_to_ask_RAM, Miss0, Miss1);
  assign or_3_out = multiplexer_1_out | register_1_q;  // OR_Gate or_3, 32 bits wide
  Multiplexer #(.width(32), .disabled(0), .enable("false")) multiplexer_2 (
    .in0(or_3_out), .in1(multiplexer_1_out), .out(Data__Data_output), .sel(IorDS));
  Multiplexer #(.disabled(0), .enable("false")) multiplexer_3 (
    .in0(SD), .in1(1'b0), .out(R_W__0_to_read_from_RAM__1_to_write_in_RAM), .sel(Read));
  Multiplexer #(.width(32), .disabled(0), .enable("false")) multiplexer_4 (
    .in0(Data_0_2), .in1(Data_0), .out(D0), .sel(Ram));
  Multiplexer #(.width(32), .disabled(0), .enable("false")) multiplexer_5 (
    .in0(Data_2_2), .in1(Data_2), .out(D2), .sel(Ram));
  Decoder #(.select(2), .disabled(0), .enable("false")) decoder_1 (
    .out0(decoder_1_out0[0]), .out1(decoder_1_out0[1]), .out2(decoder_1_out0[2]), .out3(decoder_1_out0[3]),
    .sel(Address__Address_in_RAM_to_use[3:2]));
  Comparator #(.width(10)) comparator_1 (
    .a(TagOut), .b(Address__Address_in_RAM_to_use[19:10]), .eq(comparator_1_eq));  // open: gt, lt
  Multiplexer #(.select(2), .disabled(0), .enable("false")) multiplexer_6 (
    .in0(Mask__Mask_to_signal_writing_rules_for_RAM[0]), .in1(Mask__Mask_to_signal_writing_rules_for_RAM[1]),
    .in2(Mask__Mask_to_signal_writing_rules_for_RAM[2]), .in3(Mask__Mask_to_signal_writing_rules_for_RAM[3]),
    .out(multiplexer_6_out), .sel(Address__Address_in_RAM_to_use[3:2]));
  Comparator #(.width(10)) comparator_2 (
    .a(TagOut), .b(Address__Address_in_RAM_to_use[19:10]), .eq(comparator_2_eq));  // open: gt, lt
  Multiplexer #(.width(4), .disabled(0), .enable("false")) multiplexer_7 (
    .in0(decoder_1_out0), .in1(not_1_out), .out(MaskD), .sel(Ram));
  not not_1 (not_1_out[0], Mask__Mask_to_signal_writing_rules_for_RAM[0]);
  not not_2 (not_1_out[1], Mask__Mask_to_signal_writing_rules_for_RAM[1]);
  not not_3 (not_1_out[2], Mask__Mask_to_signal_writing_rules_for_RAM[2]);
  not not_4 (not_1_out[3], Mask__Mask_to_signal_writing_rules_for_RAM[3]);
  and and_1 (SD, Dirty, not_5_out);
  not not_5 (not_5_out, comparator_1_eq);
  and and_2 (Val, multiplexer_6_out, comparator_2_eq);
  D_Flip_Flop IDLE (.clk(Clk), .D(or_4_out), .Q(IDLE_q), .preset(Rst));  // open: Qn, en, reset
  Demultiplexer #(.disabled(0), .enable("false")) demultiplexer_1 (
    .out0(demultiplexer_1_out0), .out1(demultiplexer_1_out1), .in(IDLE_q),
    .sel(CS__Chip_Selector__when_1_the_cache_detectecs_a_R_W_command));
  or or_4 (or_4_out, demultiplexer_1_out0, WriteD, ReadD);
  Multiplexer #(.width(32), .disabled(0), .enable("false")) multiplexer_8 (
    .in0(Data_1_2), .in1(Data_1), .out(D1), .sel(Ram));
  Multiplexer #(.width(32), .disabled(0), .enable("false")) multiplexer_9 (
    .in0(Data_3_2), .in1(Data_3), .out(D3), .sel(Ram));
  Demultiplexer #(.disabled(0), .enable("false")) demultiplexer_2 (
    .out0(demultiplexer_2_out0), .out1(Miss0), .in(demultiplexer_1_out1), .sel(SD));
  or or_5 (ReadD, Ram, Hit0);
  Multiplexer #(.width(32), .disabled(0), .enable("false")) multiplexer_10 (
    .in0(Data__Data_to_Write), .in1(Data_0), .out(D0D), .sel(Ram));
  Multiplexer #(.width(32), .disabled(0), .enable("false")) multiplexer_11 (
    .in0(Data__Data_to_Write), .in1(Data_2), .out(D2D), .sel(Ram));
  RegisterFile registerfile_1 (
    .EW(or_8_out), .Index(Address__Address_in_RAM_to_use[9:4]), .Data_0(D0D), .Data_1(D1D), .Data_2(D2D),
    .Data_3(D3D), .Clk(Clk), .Rst(Rst), .Mask(MaskD), .Tag(Address__Address_in_RAM_to_use[19:10]),
    .Validate(Vd), .Read_Ram(Ram), .Tag_2(TagOut), .Data_0_2(Data_0_2), .Data_1_2(Data_1_2),
    .Data_2_2(Data_2_2), .Data_3_2(Data_3_2), .Validity(Mask__Mask_to_signal_writing_rules_for_RAM),
    .Dirty(Dirty));
  or or_6 (Write, demultiplexer_4_out1, Miss0);
  D_Flip_Flop BusyR (.clk(Clk), .D(Read), .Q(BusyR_q), .reset(Rst));  // open: Qn, preset, en
  Demultiplexer #(.disabled(0), .enable("false")) demultiplexer_3 (
    .out0(Ram), .out1(demultiplexer_3_out1), .in(BusyR_q),
    .sel(Busy__Signal_of_RAM_in_use__When_Chache_asks_to_write_or_read_RAM_it_waits_for_this_to_become_0_once_it_finish));
  or or_7 (Busy__Signals_that_RAM_is_in_use, Write, Read);
  or or_8 (or_8_out, Ram, WriteD);
  D_Flip_Flop BusyW (.clk(Clk), .D(Write), .Q(BusyW_q), .reset(Rst));  // open: Qn, preset, en
  Demultiplexer #(.disabled(0), .enable("false")) demultiplexer_4 (
    .out0(Vd), .out1(demultiplexer_4_out1), .in(BusyW_q),
    .sel(Busy__Signal_of_RAM_in_use__When_Chache_asks_to_write_or_read_RAM_it_waits_for_this_to_become_0_once_it_finish));
  Demultiplexer #(.disabled(0), .enable("false")) demultiplexer_5 (
    .out0(Miss1), .out1(Hit0), .in(decoder_2_out0), .sel(Val));
  or or_9 (Read, Miss1, demultiplexer_3_out1);
  Multiplexer #(.width(32), .disabled(0), .enable("false")) multiplexer_12 (
    .in0(Data__Data_to_Write), .in1(Data_1), .out(D1D), .sel(Ram));
  Multiplexer #(.width(32), .disabled(0), .enable("false")) multiplexer_13 (
    .in0(Data__Data_to_Write), .in1(Data_3), .out(D3D), .sel(Ram));
  Decoder #(.disabled(0)) decoder_2 (
    .out0(decoder_2_out0), .out1(WriteD), .sel(R_W__0_to_read__1_to_write), .en(or_10_out));
  Multiplexer #(.width(10), .disabled(0), .enable("false")) multiplexer_14 (
    .in0(Address__Address_in_RAM_to_use[19:10]), .in1(TagOut), .out(Address__Address_to_usee_in_RAM[19:10]),
    .sel(Write));
  or or_10 (or_10_out, Vd, demultiplexer_2_out0);

  assign {Address__Address_to_usee_in_RAM[31:20], Address__Address_to_usee_in_RAM[9:0]} = {{12{1'b0}}, Address__Address_in_RAM_to_use[9:4], 4'b0000};
  assign CS__Signals_when_cache_wants_RAM_to_R_W = Busy__Signals_that_RAM_is_in_use;

  // Other names for the same wires on the sheet: Bank[1:0] = Address__Address_in_RAM_to_use[3:2];
  //   Tag[9:0] = Address__Address_in_RAM_to_use[19:10]; Index[5:0] = Address__Address_in_RAM_to_use[9:4];
  //   T[9:0] = Address__Address_to_usee_in_RAM[19:10];
  //   Busy = Busy__Signal_of_RAM_in_use__When_Chache_asks_to_write_or_read_RAM_it_waits_for_this_to_become_0_once_it_finish;
  //   CS = CS__Chip_Selector__when_1_the_cache_detectecs_a_R_W_command; CSR = Busy__Signals_that_RAM_is_in_use;
  //   Data[31:0] = Data__Data_to_Write; Data0[31:0] = Data_0_2; Data1[31:0] = Data_1_2; Data2[31:0] = Data_2_2;
  //   Data3[31:0] = Data_3_2; R_W = R_W__0_to_read__1_to_write;
  //   Validity[3:0] = Mask__Mask_to_signal_writing_rules_for_RAM

  // Notes on the sheet:
  //   Input
  //   Output
  //   Validators
  //   Circuit
  //   Multiplexors
  //   Register File
endmodule

module RegisterFile (
  input  EW,
  input  [5:0] Index,
  input  [31:0] Data_0,
  input  [31:0] Data_1,
  input  [31:0] Data_2,
  input  [31:0] Data_3,
  input  Clk,
  input  Rst,
  input  [3:0] Mask,
  input  [9:0] Tag,
  input  Validate,
  input  Read_Ram,
  output [9:0] Tag_2,
  output [31:0] Data_0_2,
  output [31:0] Data_1_2,
  output [31:0] Data_2_2,
  output [31:0] Data_3_2,
  output [3:0] Validity,
  output Dirty
);

  wire and_1_out, and_2_out, Dirty0, Dirty1, not_1_out;
  wire [3:0] Validity0, Validity1;
  wire [9:0] Tag0, Tag1;
  wire [31:0] Data00, Data01, Data10, Data11, Data20, Data21, Data30, Data31;

  Multiplexer #(.width(10), .disabled(0), .enable("false")) multiplexer_1 (
    .in0(Tag0), .in1(Tag1), .out(Tag_2), .sel(Index[5]));
  Multiplexer #(.width(32), .disabled(0), .enable("false")) multiplexer_2 (
    .in0(Data00), .in1(Data01), .out(Data_0_2), .sel(Index[5]));
  Multiplexer #(.width(32), .disabled(0), .enable("false")) multiplexer_3 (
    .in0(Data10), .in1(Data11), .out(Data_1_2), .sel(Index[5]));
  Multiplexer #(.width(32), .disabled(0), .enable("false")) multiplexer_4 (
    .in0(Data20), .in1(Data21), .out(Data_2_2), .sel(Index[5]));
  Multiplexer #(.width(32), .disabled(0), .enable("false")) multiplexer_5 (
    .in0(Data30), .in1(Data31), .out(Data_3_2), .sel(Index[5]));
  Multiplexer #(.width(4), .disabled(0), .enable("false")) multiplexer_6 (
    .in0(Validity0), .in1(Validity1), .out(Validity), .sel(Index[5]));
  Multiplexer #(.disabled(0), .enable("false")) multiplexer_7 (.in0(Dirty0), .in1(Dirty1), .out(Dirty), .sel(Index[5]));
  not not_1 (not_1_out, Index[5]);
  and and_1 (and_1_out, EW, not_1_out);
  and and_2 (and_2_out, EW, Index[5]);
  Register5 register5_1 (
    .EW(and_1_out), .Index(Index[4:0]), .Data_0(Data_0), .Data_1(Data_1), .Data_2(Data_2), .Data_3(Data_3),
    .Clk(Clk), .Rst(Rst), .Mask(Mask), .Tag(Tag), .Validate(Validate), .Read_Ram(Read_Ram), .Tag_2(Tag0),
    .Data_0_2(Data00), .Data_1_2(Data10), .Data_2_2(Data20), .Data_3_2(Data30), .Validity(Validity0),
    .Dirty(Dirty0));
  Register5 register5_2 (
    .EW(and_2_out), .Index(Index[4:0]), .Data_0(Data_0), .Data_1(Data_1), .Data_2(Data_2), .Data_3(Data_3),
    .Clk(Clk), .Rst(Rst), .Mask(Mask), .Tag(Tag), .Validate(Validate), .Read_Ram(Read_Ram), .Tag_2(Tag1),
    .Data_0_2(Data01), .Data_1_2(Data11), .Data_2_2(Data21), .Data_3_2(Data31), .Validity(Validity1),
    .Dirty(Dirty1));

  // Other names for the same wires on the sheet: Index_1[4:0] = Index[4:0]; Index_t = Index[5]; TagD[9:0] = Tag
endmodule

module Register5 (
  input  EW,
  input  [4:0] Index,
  input  [31:0] Data_0,
  input  [31:0] Data_1,
  input  [31:0] Data_2,
  input  [31:0] Data_3,
  input  Clk,
  input  Rst,
  input  [3:0] Mask,
  input  [9:0] Tag,
  input  Validate,
  input  Read_Ram,
  output [9:0] Tag_2,
  output [31:0] Data_0_2,
  output [31:0] Data_1_2,
  output [31:0] Data_2_2,
  output [31:0] Data_3_2,
  output [3:0] Validity,
  output Dirty
);

  wire and_1_out, and_2_out, Dirty0, Dirty1, not_1_out;
  wire [3:0] Validity0, Validity1;
  wire [9:0] Tag0, Tag1;
  wire [31:0] Data00, Data01, Data10, Data11, Data20, Data21, Data30, Data31;

  Multiplexer #(.width(10), .disabled(0), .enable("false")) multiplexer_1 (
    .in0(Tag0), .in1(Tag1), .out(Tag_2), .sel(Index[4]));
  Multiplexer #(.width(32), .disabled(0), .enable("false")) multiplexer_2 (
    .in0(Data00), .in1(Data01), .out(Data_0_2), .sel(Index[4]));
  Multiplexer #(.width(32), .disabled(0), .enable("false")) multiplexer_3 (
    .in0(Data10), .in1(Data11), .out(Data_1_2), .sel(Index[4]));
  Multiplexer #(.width(32), .disabled(0), .enable("false")) multiplexer_4 (
    .in0(Data20), .in1(Data21), .out(Data_2_2), .sel(Index[4]));
  Multiplexer #(.width(32), .disabled(0), .enable("false")) multiplexer_5 (
    .in0(Data30), .in1(Data31), .out(Data_3_2), .sel(Index[4]));
  Multiplexer #(.width(4), .disabled(0), .enable("false")) multiplexer_6 (
    .in0(Validity0), .in1(Validity1), .out(Validity), .sel(Index[4]));
  Multiplexer #(.disabled(0), .enable("false")) multiplexer_7 (.in0(Dirty0), .in1(Dirty1), .out(Dirty), .sel(Index[4]));
  not not_1 (not_1_out, Index[4]);
  and and_1 (and_1_out, EW, not_1_out);
  and and_2 (and_2_out, EW, Index[4]);
  Register4 register4_1 (
    .EW(and_1_out), .Index(Index[3:0]), .Data_0(Data_0), .Data_1(Data_1), .Data_2(Data_2), .Data_3(Data_3),
    .Clk(Clk), .Rst(Rst), .Mask(Mask), .Tag(Tag), .Validate(Validate), .Read_Ram(Read_Ram), .Tag_2(Tag0),
    .Data_0_2(Data00), .Data_1_2(Data10), .Data_2_2(Data20), .Data_3_2(Data30), .Validity(Validity0),
    .Dirty(Dirty0));
  Register4 register4_2 (
    .EW(and_2_out), .Index(Index[3:0]), .Data_0(Data_0), .Data_1(Data_1), .Data_2(Data_2), .Data_3(Data_3),
    .Clk(Clk), .Rst(Rst), .Mask(Mask), .Tag(Tag), .Validate(Validate), .Read_Ram(Read_Ram), .Tag_2(Tag1),
    .Data_0_2(Data01), .Data_1_2(Data11), .Data_2_2(Data21), .Data_3_2(Data31), .Validity(Validity1),
    .Dirty(Dirty1));

  // Other names for the same wires on the sheet: Index_1[3:0] = Index[3:0]; Index_t = Index[4]; TagD[9:0] = Tag
endmodule

module Register4 (
  input  EW,
  input  [3:0] Index,
  input  [31:0] Data_0,
  input  [31:0] Data_1,
  input  [31:0] Data_2,
  input  [31:0] Data_3,
  input  Clk,
  input  Rst,
  input  [3:0] Mask,
  input  [9:0] Tag,
  input  Validate,
  input  Read_Ram,
  output [9:0] Tag_2,
  output [31:0] Data_0_2,
  output [31:0] Data_1_2,
  output [31:0] Data_2_2,
  output [31:0] Data_3_2,
  output [3:0] Validity,
  output Dirty
);

  wire and_1_out, and_2_out, Dirty0, Dirty1, not_1_out;
  wire [3:0] Validity0, Validity1;
  wire [9:0] Tag0, Tag1;
  wire [31:0] Data00, Data01, Data10, Data11, Data20, Data21, Data30, Data31;

  Multiplexer #(.width(10), .disabled(0), .enable("false")) multiplexer_1 (
    .in0(Tag0), .in1(Tag1), .out(Tag_2), .sel(Index[3]));
  Multiplexer #(.width(32), .disabled(0), .enable("false")) multiplexer_2 (
    .in0(Data00), .in1(Data01), .out(Data_0_2), .sel(Index[3]));
  Multiplexer #(.width(32), .disabled(0), .enable("false")) multiplexer_3 (
    .in0(Data10), .in1(Data11), .out(Data_1_2), .sel(Index[3]));
  Multiplexer #(.width(32), .disabled(0), .enable("false")) multiplexer_4 (
    .in0(Data20), .in1(Data21), .out(Data_2_2), .sel(Index[3]));
  Multiplexer #(.width(32), .disabled(0), .enable("false")) multiplexer_5 (
    .in0(Data30), .in1(Data31), .out(Data_3_2), .sel(Index[3]));
  Multiplexer #(.width(4), .disabled(0), .enable("false")) multiplexer_6 (
    .in0(Validity0), .in1(Validity1), .out(Validity), .sel(Index[3]));
  Multiplexer #(.disabled(0), .enable("false")) multiplexer_7 (.in0(Dirty0), .in1(Dirty1), .out(Dirty), .sel(Index[3]));
  not not_1 (not_1_out, Index[3]);
  and and_1 (and_1_out, EW, not_1_out);
  and and_2 (and_2_out, EW, Index[3]);
  Register3 register3_1 (
    .EW(and_1_out), .Index(Index[2:0]), .Data_0(Data_0), .Data_1(Data_1), .Data_2(Data_2), .Data_3(Data_3),
    .Clk(Clk), .Rst(Rst), .Mask(Mask), .Tag(Tag), .Validate(Validate), .Read_Ram(Read_Ram), .Tag_2(Tag0),
    .Data_0_2(Data00), .Data_1_2(Data10), .Data_2_2(Data20), .Data_3_2(Data30), .Validity(Validity0),
    .Dirty(Dirty0));
  Register3 register3_2 (
    .EW(and_2_out), .Index(Index[2:0]), .Data_0(Data_0), .Data_1(Data_1), .Data_2(Data_2), .Data_3(Data_3),
    .Clk(Clk), .Rst(Rst), .Mask(Mask), .Tag(Tag), .Validate(Validate), .Read_Ram(Read_Ram), .Tag_2(Tag1),
    .Data_0_2(Data01), .Data_1_2(Data11), .Data_2_2(Data21), .Data_3_2(Data31), .Validity(Validity1),
    .Dirty(Dirty1));

  // Other names for the same wires on the sheet: Index_1[2:0] = Index[2:0]; Index_t = Index[3]; TagD[9:0] = Tag
endmodule

module Register3 (
  input  EW,
  input  [2:0] Index,
  input  [31:0] Data_0,
  input  [31:0] Data_1,
  input  [31:0] Data_2,
  input  [31:0] Data_3,
  input  Clk,
  input  Rst,
  input  [3:0] Mask,
  input  [9:0] Tag,
  input  Validate,
  input  Read_Ram,
  output [9:0] Tag_2,
  output [31:0] Data_0_2,
  output [31:0] Data_1_2,
  output [31:0] Data_2_2,
  output [31:0] Data_3_2,
  output [3:0] Validity,
  output Dirty
);

  wire and_1_out, and_2_out, Dirty0, Dirty1, not_1_out;
  wire [3:0] Validity0, Validity1;
  wire [9:0] Tag0, Tag1;
  wire [31:0] Data00, Data01, Data10, Data11, Data20, Data21, Data30, Data31;

  Multiplexer #(.width(10), .disabled(0), .enable("false")) multiplexer_1 (
    .in0(Tag0), .in1(Tag1), .out(Tag_2), .sel(Index[2]));
  Multiplexer #(.width(32), .disabled(0), .enable("false")) multiplexer_2 (
    .in0(Data00), .in1(Data01), .out(Data_0_2), .sel(Index[2]));
  Multiplexer #(.width(32), .disabled(0), .enable("false")) multiplexer_3 (
    .in0(Data10), .in1(Data11), .out(Data_1_2), .sel(Index[2]));
  Multiplexer #(.width(32), .disabled(0), .enable("false")) multiplexer_4 (
    .in0(Data20), .in1(Data21), .out(Data_2_2), .sel(Index[2]));
  Multiplexer #(.width(32), .disabled(0), .enable("false")) multiplexer_5 (
    .in0(Data30), .in1(Data31), .out(Data_3_2), .sel(Index[2]));
  Multiplexer #(.width(4), .disabled(0), .enable("false")) multiplexer_6 (
    .in0(Validity0), .in1(Validity1), .out(Validity), .sel(Index[2]));
  Multiplexer #(.disabled(0), .enable("false")) multiplexer_7 (.in0(Dirty0), .in1(Dirty1), .out(Dirty), .sel(Index[2]));
  not not_1 (not_1_out, Index[2]);
  and and_1 (and_1_out, EW, not_1_out);
  and and_2 (and_2_out, EW, Index[2]);
  Register2 register2_1 (
    .EW(and_1_out), .Index(Index[1:0]), .Data_0(Data_0), .Data_1(Data_1), .Data_2(Data_2), .Data_3(Data_3),
    .Clk(Clk), .Rst(Rst), .Mask(Mask), .Tag(Tag), .Validate(Validate), .Read_Ram(Read_Ram), .Tag_2(Tag0),
    .Data_0_2(Data00), .Data_1_2(Data10), .Data_2_2(Data20), .Data_3_2(Data30), .Validity(Validity0),
    .Dirty(Dirty0));
  Register2 register2_2 (
    .EW(and_2_out), .Index(Index[1:0]), .Data_0(Data_0), .Data_1(Data_1), .Data_2(Data_2), .Data_3(Data_3),
    .Clk(Clk), .Rst(Rst), .Mask(Mask), .Tag(Tag), .Validate(Validate), .Read_Ram(Read_Ram), .Tag_2(Tag1),
    .Data_0_2(Data01), .Data_1_2(Data11), .Data_2_2(Data21), .Data_3_2(Data31), .Validity(Validity1),
    .Dirty(Dirty1));

  // Other names for the same wires on the sheet: Index_1[1:0] = Index[1:0]; Index_t = Index[2]; TagD[9:0] = Tag
endmodule

module Register2 (
  input  EW,
  input  [1:0] Index,
  input  [31:0] Data_0,
  input  [31:0] Data_1,
  input  [31:0] Data_2,
  input  [31:0] Data_3,
  input  Clk,
  input  Rst,
  input  [3:0] Mask,
  input  [9:0] Tag,
  input  Validate,
  input  Read_Ram,
  output [9:0] Tag_2,
  output [31:0] Data_0_2,
  output [31:0] Data_1_2,
  output [31:0] Data_2_2,
  output [31:0] Data_3_2,
  output [3:0] Validity,
  output Dirty
);

  wire and_1_out, and_2_out, Dirty0, Dirty1, not_1_out;
  wire [3:0] Validity0, Validity1;
  wire [9:0] Tag0, Tag1;
  wire [31:0] Data00, Data01, Data10, Data11, Data20, Data21, Data30, Data31;

  Multiplexer #(.width(10), .disabled(0), .enable("false")) multiplexer_1 (
    .in0(Tag0), .in1(Tag1), .out(Tag_2), .sel(Index[1]));
  Multiplexer #(.width(32), .disabled(0), .enable("false")) multiplexer_2 (
    .in0(Data00), .in1(Data01), .out(Data_0_2), .sel(Index[1]));
  Multiplexer #(.width(32), .disabled(0), .enable("false")) multiplexer_3 (
    .in0(Data10), .in1(Data11), .out(Data_1_2), .sel(Index[1]));
  Multiplexer #(.width(32), .disabled(0), .enable("false")) multiplexer_4 (
    .in0(Data20), .in1(Data21), .out(Data_2_2), .sel(Index[1]));
  Multiplexer #(.width(32), .disabled(0), .enable("false")) multiplexer_5 (
    .in0(Data30), .in1(Data31), .out(Data_3_2), .sel(Index[1]));
  Multiplexer #(.width(4), .disabled(0), .enable("false")) multiplexer_6 (
    .in0(Validity0), .in1(Validity1), .out(Validity), .sel(Index[1]));
  Multiplexer #(.disabled(0), .enable("false")) multiplexer_7 (.in0(Dirty0), .in1(Dirty1), .out(Dirty), .sel(Index[1]));
  not not_1 (not_1_out, Index[1]);
  and and_1 (and_1_out, EW, not_1_out);
  and and_2 (and_2_out, EW, Index[1]);
  Register1 register1_1 (
    .EW(and_1_out), .Index(Index[0]), .Data_0(Data_0), .Data_1(Data_1), .Data_2(Data_2), .Data_3(Data_3),
    .Clk(Clk), .Rst(Rst), .Mask(Mask), .Tag(Tag), .Validate(Validate), .Read_Ram(Read_Ram), .Tag_2(Tag0),
    .Data_0_2(Data00), .Data_1_2(Data10), .Data_2_2(Data20), .Data_3_2(Data30), .Validity(Validity0),
    .Dirty(Dirty0));
  Register1 register1_2 (
    .EW(and_2_out), .Index(Index[0]), .Data_0(Data_0), .Data_1(Data_1), .Data_2(Data_2), .Data_3(Data_3),
    .Clk(Clk), .Rst(Rst), .Mask(Mask), .Tag(Tag), .Validate(Validate), .Read_Ram(Read_Ram), .Tag_2(Tag1),
    .Data_0_2(Data01), .Data_1_2(Data11), .Data_2_2(Data21), .Data_3_2(Data31), .Validity(Validity1),
    .Dirty(Dirty1));

  // Other names for the same wires on the sheet: Index_1 = Index[0]; Index_t = Index[1]; TagD[9:0] = Tag
endmodule

module Register1 (
  input  EW,
  input  Index,
  input  [31:0] Data_0,
  input  [31:0] Data_1,
  input  [31:0] Data_2,
  input  [31:0] Data_3,
  input  Clk,
  input  Rst,
  input  [3:0] Mask,
  input  [9:0] Tag,
  input  Validate,
  input  Read_Ram,
  output [9:0] Tag_2,
  output [31:0] Data_0_2,
  output [31:0] Data_1_2,
  output [31:0] Data_2_2,
  output [31:0] Data_3_2,
  output [3:0] Validity,
  output Dirty
);

  wire and_1_out, and_2_out, Dirty0, Dirty1, not_1_out;
  wire [3:0] Validity0, Validity1;
  wire [9:0] Tag0, Tag1;
  wire [31:0] Data00, Data01, Data10, Data11, Data20, Data21, Data30, Data31;

  Multiplexer #(.width(10), .disabled(0), .enable("false")) multiplexer_1 (
    .in0(Tag0), .in1(Tag1), .out(Tag_2), .sel(Index));
  Multiplexer #(.width(32), .disabled(0), .enable("false")) multiplexer_2 (
    .in0(Data00), .in1(Data01), .out(Data_0_2), .sel(Index));
  Multiplexer #(.width(32), .disabled(0), .enable("false")) multiplexer_3 (
    .in0(Data10), .in1(Data11), .out(Data_1_2), .sel(Index));
  Multiplexer #(.width(32), .disabled(0), .enable("false")) multiplexer_4 (
    .in0(Data20), .in1(Data21), .out(Data_2_2), .sel(Index));
  Multiplexer #(.width(32), .disabled(0), .enable("false")) multiplexer_5 (
    .in0(Data30), .in1(Data31), .out(Data_3_2), .sel(Index));
  Multiplexer #(.width(4), .disabled(0), .enable("false")) multiplexer_6 (
    .in0(Validity0), .in1(Validity1), .out(Validity), .sel(Index));
  Multiplexer #(.disabled(0), .enable("false")) multiplexer_7 (.in0(Dirty0), .in1(Dirty1), .out(Dirty), .sel(Index));
  not not_1 (not_1_out, Index);
  and and_1 (and_1_out, EW, not_1_out);
  and and_2 (and_2_out, EW, Index);
  Register register_1 (
    .EW(and_1_out), .Data_0(Data_0), .Data_1(Data_1), .Data_2(Data_2), .Data_3(Data_3), .Clk(Clk), .Rst(Rst),
    .Mask(Mask), .Tag(Tag), .Validate(Validate), .Read_Ram(Read_Ram), .Tag_2(Tag0), .Data_0_2(Data00),
    .Data_1_2(Data10), .Data_2_2(Data20), .Data_3_2(Data30), .Validity(Validity0), .Dirty(Dirty0));
  Register register_2 (
    .EW(and_2_out), .Data_0(Data_0), .Data_1(Data_1), .Data_2(Data_2), .Data_3(Data_3), .Clk(Clk), .Rst(Rst),
    .Mask(Mask), .Tag(Tag), .Validate(Validate), .Read_Ram(Read_Ram), .Tag_2(Tag1), .Data_0_2(Data01),
    .Data_1_2(Data11), .Data_2_2(Data21), .Data_3_2(Data31), .Validity(Validity1), .Dirty(Dirty1));

  // Other names for the same wires on the sheet: TagD[9:0] = Tag
endmodule

module Register (
  input  EW,
  input  [31:0] Data_0,
  input  [31:0] Data_1,
  input  [31:0] Data_2,
  input  [31:0] Data_3,
  input  Clk,
  input  Rst,
  input  [3:0] Mask,
  input  [9:0] Tag,
  input  Validate,
  input  Read_Ram,
  output [9:0] Tag_2,
  output [31:0] Data_0_2,
  output [31:0] Data_1_2,
  output [31:0] Data_2_2,
  output [31:0] Data_3_2,
  output [3:0] Validity,
  output Dirty
);

  wire and_2_out, and_3_out, and_4_out, comparator_1_eq, nor_1_out, not_1_out, or_1_out;
  wire [3:0] bit_extender_1_out, E, multiplexer_1_out, or_2_out;

  assign bit_extender_1_out = {{3{EW}}, EW};  // Bit_Extender bit_extender_1
  assign E = Mask & bit_extender_1_out;  // AND_Gate and_1, 4 bits wide
  not not_1 (not_1_out, Dirty);
  or or_1 (or_1_out, Read_Ram, comparator_1_eq);
  Comparator #(.width(4)) comparator_1 (.a(E), .b(4'b0000), .eq(comparator_1_eq));  // open: gt, lt
  Register_part #(.width(32)) Data0 (.D(Data_0), .en(E[0]), .Q(Data_0_2), .clk(Clk), .clr(Rst));
  Register_part #(.width(32)) Data2 (.D(Data_2), .en(E[2]), .Q(Data_2_2), .clk(Clk), .clr(Rst));
  Register_part #(.width(10)) u_Tag (.D(Tag), .en(EW), .Q(Tag_2), .clk(Clk), .clr(Rst));
  and and_2 (and_2_out, not_1_out, or_1_out);
  assign or_2_out = Validity | E;  // OR_Gate or_2, 4 bits wide
  Multiplexer #(.width(4), .disabled(0), .enable("false")) multiplexer_1 (
    .in0(or_2_out), .in1(E), .out(multiplexer_1_out), .sel(Validate));
  and and_3 (and_3_out, E[0], E[1], Read_Ram, E[2], E[3]);
  nor nor_1 (nor_1_out, and_3_out, and_2_out, and_4_out);
  and and_4 (and_4_out, Validate, comparator_1_eq);
  Register_part #(.width(32)) Data1 (.D(Data_1), .en(E[1]), .Q(Data_1_2), .clk(Clk), .clr(Rst));
  Register_part #(.width(32)) Data3 (.D(Data_3), .en(E[3]), .Q(Data_3_2), .clk(Clk), .clr(Rst));
  Register_part #(.width(4)) u_Validity (.D(multiplexer_1_out), .en(1'b1), .Q(Validity), .clk(Clk), .clr(Rst));
  Register_part #(.width(1)) u_Dirty (.D(nor_1_out), .en(EW), .Q(Dirty), .clk(Clk), .clr(Rst));

  // Other names for the same wires on the sheet: Data0[31:0] = Data_0_2; Data1[31:0] = Data_1_2;
  //   Data2[31:0] = Data_2_2; Data3[31:0] = Data_3_2; Tag_t[9:0] = Tag_2; TagD[9:0] = Tag
endmodule
