// Logisim project ControlUnit.circ as structural Verilog: 16 circuits, main circuit ControlUnit
module ControlUnit (
  input  [5:0] OpCode,
  input  [5:0] FunCode,
  input  Clk,
  input  Rst,
  input  ZF,
  input  NF,
  input  Busy,
  output STOP,
  output ETTY,
  output CS,
  output RW,
  output SPDir,
  output EPC,
  output EIR,
  output ER,
  output EMDR,
  output EALUOut,
  output EHi,
  output ELo,
  output [1:0] SW3,
  output EW,
  output SSPR,
  output SSPW,
  output [3:0] SALU,
  output [1:0] SA,
  output [1:0] SB,
  output EB,
  output SD,
  output IorDS,
  output SWA,
  output SMR,
  output SIS,
  output EKBD
);

  wire and_1_out, and_2_out, and_3_out, and_4_out, and_5_out, and_6_out, and_7_out, and_8_out, Busy_t,
       comparator_4_eq, comparator_5_eq, CS5, CS6, CS12, demultiplexer_1_out1, EALU1, EALU2, EALU10, EALU11,
       EALU12, EB0, EB1, EB2, EB4, EB5, EB6, EB10, EB11, EB12, EB13, ED, EI, EJ, EMD5, EMD12, End, End0,
       End4, End13, END_q, EO2, EO_2, EO_2_t, EPC0, EPC4, EPC11, EPC13, ER1, ER2, ER4, ER5, ER6, ER9, ER10,
       ER11, ER12, ERb, ERs, EW1, EW3, EW5, EW6, EW7, EW8, EW10, EW12, halt, IALU, Ibf, Ilw_sw, Inst, Inst_q,
       IOp, IorDS5, IorDS6, IorDS12, jr, kbd, mfhi, mflo, nop, or_11_out, or_24_out, PC1, PC2, PC3, PC5, PC6,
       PC7, PC8, PC9, PC10, PC11, PC12, PCnop, pop, push, R_W5, R_W6, R_W12, rnd, SD5, SD6, SD12, SIS10,
       SIS12, SMR5, SMR7, SMR12, SPC, SSPR5, SSPR6, SSPW5, SSPW6, Start, SWA5, SWA6, SWA10, SWA12, tty, VOp,
       Wait_for_Ram_2_q, Wait_for_Ram_q;
  wire [1:0] OpType, SA0, SA1, SA2, SA4, SA5, SA6, SA10, SA11, SA12, SA13, SB0, SB1, SB2, SB4, SB5, SB6,
       SB10, SB11, SB12, SB13, SW1, SW3_t, SW5, SW6, SW7, SW10, SW12;
  wire [3:0] OpS, SALU0, SALU1, SALU2, SALU4, SALU5, SALU6, SALU10, SALU11, SALU12, SALU13;

  Pull_Resistor pull_resistor_1 (.node(OpCode));
  Pull_Resistor pull_resistor_2 (.node(FunCode));
  Pull_Resistor pull_resistor_3 (.node(ZF));
  Pull_Resistor pull_resistor_4 (.node(NF));
  Pull_Resistor pull_resistor_5 (.node(Busy));
  Multiplexer #(.disabled(0), .enable("false")) multiplexer_1 (.in0(Busy), .in1(1'b0), .out(Busy_t), .sel(Start));
  D_Flip_Flop IDLE (.clk(Clk), .D(1'b0), .Q(Start), .preset(Rst));  // open: Qn, en, reset
  OpDecoder opdecoder_1 (
    .OpCode(OpCode), .FunCode(FunCode),
    .Type__0_for_basic_type_R__and_1_for_special_R__2_for_type_I_and_3_for_type_J(OpType),
    .OpS__Selector_of_the_operation(OpS), .Valid__1_if_the_OC_and_FC_belong_to_a_valid_operation(VOp));
  Decoder #(.select(2), .disabled(0)) decoder_1 (.out0(ERb), .out1(ERs), .out2(EI), .out3(EJ), .sel(OpType), .en(ED));
  D_Flip_Flop u_END (.clk(Clk), .D(End), .Q(END_q), .reset(Rst));  // open: Qn, preset, en
  or or_1 (Inst, END_q, Start, demultiplexer_1_out1);
  Comparator #(.width(2), .mode("unsigned")) comparator_1 (.a(2'b10), .b(OpS[3:2]), .gt(EO_2), .eq(EO2), .lt(EO_2_t));
  Comparator #(.width(4), .mode("unsigned")) comparator_2 (.a(OpS), .b(4'b0110), .lt(IALU));  // open: gt, eq
  Comparator #(.width(4), .mode("unsigned")) comparator_3 (.a(OpS), .b(4'b1010), .gt(Ilw_sw));  // open: eq, lt
  Decoder #(.select(4), .disabled(0)) decoder_2 (
    .out0(pop), .out1(push), .out2(halt), .out3(rnd), .out4(kbd), .out5(tty), .sel(OpS), .en(ERs));  // open: out6, out7, out8, out9, out10, out11, out12, out13, out14, out15
  or or_2 (EPC, EPC0, EPC4, EPC11, EPC13);
  or or_3 (CS, CS5, Inst, CS6, CS12);
  or or_4 (RW, R_W5, R_W6, R_W12);
  or or_5 (ER, ER1, ER2, ER4, ER5, ER6, ER9, ER10, ER11, ER12);
  or or_6 (SD, SD5, SD6, SD12);
  or or_7 (IorDS, IorDS5, IorDS6, IorDS12);
  assign SA = SA0 | SA1 | SA2 | SA4 | SA5 | SA6 | SA10 | SA11 | SA12 | SA13;  // OR_Gate or_8, 2 bits wide
  assign SB = SB0 | SB1 | SB2 | SB4 | SB5 | SB6 | SB10 | SB11 | SB12 | SB13;  // OR_Gate or_9, 2 bits wide
  or or_10 (EB, EB0, EB1, EB2, EB4, EB5, EB6, EB10, EB11, EB12, EB13);
  Demultiplexer #(.disabled(0), .enable("false")) demultiplexer_1 (
    .out0(EIR), .out1(demultiplexer_1_out1), .in(Inst_q), .sel(Busy_t));
  D_Flip_Flop u_Inst (.clk(Clk), .D(Inst), .Q(Inst_q), .reset(Rst));  // open: Qn, preset, en
  D_Flip_Flop u_SPC (.clk(Clk), .D(SPC), .Q(PCnop), .reset(Rst));  // open: Qn, preset, en
  Demultiplexer #(.disabled(0), .enable("false")) demultiplexer_2 (.out0(IOp), .out1(ED), .in(EIR), .sel(VOp));
  or or_11 (or_11_out, STOP, halt, IOp);
  or or_12 (End, End0, End4, End13);
  or or_13 (SPC, PC1, PC2, PC3, PC5, PC6, PC11, PC7, PC8, PC9, PC10, PC12);
  Decoder #(.select(2), .disabled(0)) decoder_3 (
    .out0(mfhi), .out1(mflo), .out2(nop), .out3(jr), .sel(OpS[1:0]), .en(EO_2_t));
  nor nor_1 (Ibf, IALU, Ilw_sw);
  assign SALU = SALU0 | SALU1 | SALU2 | SALU4 | SALU5 | SALU6 | SALU10 | SALU11 | SALU12 | SALU13;  // OR_Gate or_14, 4 bits wide
  or or_15 (EMDR, EMD5, EMD12);
  or or_16 (EALUOut, EALU1, EALU2, EALU11, EALU10, EALU12);
  or or_17 (EW, EW1, EW3, EW5, EW6, EW7, EW8, EW10, EW12);
  D_Flip_Flop u_Stop (.clk(Clk), .D(or_11_out), .Q(STOP), .reset(Rst));  // open: Qn, preset, en
  or or_18 (SMR, SMR5, SMR7, SMR12);
  or or_19 (SIS, SIS10, SIS12);
  or or_20 (SWA, SWA5, SWA6, SWA10, SWA12);
  or or_21 (SSPW, SSPW6, SSPW5);
  or or_22 (SSPR, SSPR5, SSPR6);
  assign SW3 = SW1 | SW3_t | SW5 | SW6 | SW7 | SW10 | SW12;  // OR_Gate or_23, 2 bits wide
  RsRnd rsrnd_1 (.Start(rnd), .SMR(SMR7), .SW3(SW7), .EW(EW7), .End(PC7));  // open: Clk, Rst
  D_Flip_Flop Wait_for_Ram (.clk(Clk), .D(pop), .Q(Wait_for_Ram_q), .reset(Rst));  // open: Qn, preset, en
  and and_1 (and_1_out, IALU, EI);
  and and_2 (and_2_out, Ilw_sw, EI);
  or or_24 (or_24_out, PCnop, and_3_out);
  and and_3 (and_3_out, ERb, nop);
  and and_4 (and_4_out, EO_2, ERb);
  and and_5 (and_5_out, EO2, ERb);
  Comparator #(.width(3), .mode("unsigned")) comparator_4 (
    .a(OpS[3:1]), .b(3'b110), .eq(comparator_4_eq));  // open: gt, lt
  Comparator #(.width(4), .mode("unsigned")) comparator_5 (.a(4'b1111), .b(OpS), .eq(comparator_5_eq));  // open: gt, lt
  RsPop rspop_1 (
    .Start(Wait_for_Ram_q), .Clk(Clk), .Rst(Rst), .Busy(Busy_t), .ER(ER5), .SSPR(SSPR5), .SA(SA5), .SB(SB5),
    .EB(EB5), .SALU(SALU5), .IorDS(IorDS5), .CS(CS5), .R_W(R_W5), .EMDR(EMD5), .SMR(SMR5), .SW3(SW5),
    .SWA(SWA5), .EW(EW5), .SSPW(SSPW5), .End(PC5), .SD(SD5));
  RsPush rspush_1 (
    .Start(push), .Clk(Clk), .Rst(Rst), .Busy(Busy_t), .ER(ER6), .SSPR(SSPR6), .SA(SA6), .SB(SB6), .EB(EB6),
    .SALU(SALU6), .SSPW(SSPW6), .SW3(SW6), .SWA(SWA6), .EW(EW6), .IorDS(IorDS6), .SD(SD6), .CS(CS6),
    .R_W(R_W6), .End(PC6), .SPDir(SPDir));
  IALU ialu_1 (
    .Start(and_1_out), .Clk(Clk), .Rst(Rst), .SALU(OpS), .ER(ER10), .SA(SA10), .SB(SB10), .EB(EB10),
    .SWA(SWA10), .SIS(SIS10), .SALU_2(SALU10), .EALU(EALU10), .SW(SW10), .EW(EW10), .End(PC10));
  and and_6 (and_6_out, Ibf, EI);
  lw_sw lw_sw_1 (
    .Start(Wait_for_Ram_2_q), .Clk(Clk), .Rst(Rst), .SALU(OpS), .Busy(Busy_t), .ER(ER12), .SA(SA12),
    .SB(SB12), .EB(EB12), .SIS(SIS12), .SALU_2(SALU12), .EALU(EALU12), .IorDS(IorDS12), .SD(SD12), .CS(CS12),
    .R_W(R_W12), .EMDR(EMD12), .SMR(SMR12), .SW3(SW12), .SWA(SWA12), .EW(EW12), .End(PC12));
  D_Flip_Flop Wait_for_Ram_2 (.clk(Clk), .D(and_2_out), .Q(Wait_for_Ram_2_q), .reset(Rst));  // open: Qn, preset, en
  j j_1 (.Start(EJ), .Clk(Clk), .Rst(Rst), .SA(SA13), .SB(SB13), .EB(EB13), .SALU(SALU13), .EPC(EPC13), .End(End13));
  nop nop_1 (
    .Start(or_24_out), .Clk(Clk), .Rst(Rst), .SA(SA0), .SB(SB0), .EB(EB0), .SALU(SALU0), .EPC(EPC0),
    .End(End0));
  RbALUResult rbaluresult_1 (
    .Start(and_4_out), .Clk(Clk), .Rst(Rst), .SALU(OpS), .ER(ER1), .SA(SA1), .SB(SB1), .EB(EB1),
    .SALU_2(SALU1), .EALU(EALU1), .SW(SW1), .EW(EW1), .End(PC1));
  RbALULoHi rbalulohi_1 (
    .Start(and_5_out), .Clk(Clk), .Rst(Rst), .SALU(OpS), .SA(SA2), .SB(SB2), .EB(EB2), .ER(ER2),
    .SALU_2(SALU2), .EALU(EALU2), .EHi(EHi), .ELo(ELo), .End(PC2));
  RbMfhi_lo rbmfhi_lo_1 (.Start(and_7_out), .Clk(Clk), .Rst(Rst), .SOp(OpS), .SW(SW3_t), .EW(EW3), .End(PC3));
  and and_7 (and_7_out, comparator_4_eq, ERb);
  jr jr_1 (
    .Start(and_8_out), .Clk(Clk), .Rst(Rst), .SA(SA4), .SB(SB4), .EB(EB4), .ER(ER4), .SALU(SALU4),
    .EPC(EPC4), .End(End4));
  and and_8 (and_8_out, comparator_5_eq, ERb);
  RsKbd rskbd_1 (.Start(kbd), .EW(EW8), .EKBD(EKBD), .End(PC8));
  Ibf ibf_1 (
    .Start(and_6_out), .Clk(Clk), .Rst(Rst), .OS(OpS), .ZF(ZF), .NF(NF), .ER(ER11), .SA(SA11), .SB(SB11),
    .EB(EB11), .SALU(SALU11), .EALU(EALU11), .EPC(EPC11), .End(PC11));
  RsTty rstty_1 (.Start(tty), .ETty(ETTY), .End(PC9), .ER(ER9));

  // Other names for the same wires on the sheet: EHi2 = EHi; EKBD8 = EKBD; ELo2 = ELo; ETTY9 = ETTY;
  //   FC[5:0] = FunCode; OC[5:0] = OpCode; SO[1:0] = OpS[1:0]; Read = EIR; SW[1:0] = SW3

  // Notes on the sheet:
  //   Input
  //   Output
  //   Initial Circuit
  //   Selector Decoder
  //   End Instruction
  //   Save PC Instruction
  //   Machines
endmodule

module OpDecoder (
  input  [5:0] OpCode,
  input  [5:0] FunCode,
  output [1:0] Type__0_for_basic_type_R__and_1_for_special_R__2_for_type_I_and_3_for_type_J,
  output [3:0] OpS__Selector_of_the_operation,
  output Valid__1_if_the_OC_and_FC_belong_to_a_valid_operation
);

  wire and_1_out, and_2_out, and_3_out, comparator_5_eq, comparator_6_eq, comparator_7_eq, comparator_8_eq,
       comparator_9_eq, comparator_10_eq, comparator_11_eq, comparator_12_eq, comparator_13_eq,
       comparator_14_eq, comparator_15_eq, comparator_16_eq, comparator_17_eq, comparator_18_eq,
       comparator_19_eq, comparator_20_eq, comparator_21_eq, comparator_22_eq, comparator_23_eq,
       comparator_24_eq, comparator_25_eq, comparator_26_eq, comparator_27_eq, comparator_28_eq,
       comparator_29_eq, comparator_30_eq, comparator_31_eq, comparator_32_eq, comparator_33_eq,
       comparator_34_eq, comparator_35_eq, comparator_36_eq, comparator_37_eq, comparator_38_eq,
       comparator_39_eq, I, J, multiplexer_1_out, multiplexer_2_out, multiplexer_3_out, multiplexer_4_out,
       multiplexer_5_out, multiplexer_6_out, Rb, Rs, Rs0, Rs1, VI, VRb, VRs;
  wire [3:0] OpSI, OpSJ, OpSRb, OpSRs;

  Comparator #(.width(6)) comparator_1 (.a(OpCode), .b(6'b000010), .eq(J));  // open: gt, lt
  Comparator #(.width(6)) comparator_2 (.a(OpCode), .b({6{1'b0}}), .eq(Rb));  // open: gt, lt
  Comparator #(.width(6)) comparator_3 (.a(OpCode), .b(6'b111000), .eq(Rs0));  // open: gt, lt
  Comparator #(.width(6)) comparator_4 (.a(OpCode), .b({6{1'b1}}), .eq(Rs1));  // open: gt, lt
  or or_1 (Rs, Rs0, Rs1);
  nor nor_1 (I, Rb, Rs, J);
  Priority_Encoder #(.select(2)) priority_encoder_1 (
    .in0(Rb), .in1(Rs), .in2(I), .in3(J),
    .out(Type__0_for_basic_type_R__and_1_for_special_R__2_for_type_I_and_3_for_type_J));  // open: gs, en_out, en_in
  Comparator #(.width(6)) comparator_5 (.a(FunCode), .b(6'b100000), .eq(comparator_5_eq));  // open: gt, lt
  Comparator #(.width(6)) comparator_6 (.a(FunCode), .b(6'b100010), .eq(comparator_6_eq));  // open: gt, lt
  Comparator #(.width(6)) comparator_7 (.a(FunCode), .b(6'b100100), .eq(comparator_7_eq));  // open: gt, lt
  Comparator #(.width(6)) comparator_8 (.a(FunCode), .b(6'b100101), .eq(comparator_8_eq));  // open: gt, lt
  Comparator #(.width(6)) comparator_9 (.a(FunCode), .b(6'b100111), .eq(comparator_9_eq));  // open: gt, lt
  Comparator #(.width(6)) comparator_10 (.a(FunCode), .b(6'b101000), .eq(comparator_10_eq));  // open: gt, lt
  Comparator #(.width(6)) comparator_11 (.a(FunCode), .b(6'b101010), .eq(comparator_11_eq));  // open: gt, lt
  Comparator #(.width(6)) comparator_12 (.a(FunCode), .b(6'b101011), .eq(comparator_12_eq));  // open: gt, lt
  Comparator #(.width(6)) comparator_13 (.a(FunCode), .b(6'b011000), .eq(comparator_13_eq));  // open: gt, lt
  Comparator #(.width(6)) comparator_14 (.a(FunCode), .b(6'b011001), .eq(comparator_14_eq));  // open: gt, lt
  Comparator #(.width(6)) comparator_15 (.a(FunCode), .b(6'b011010), .eq(comparator_15_eq));  // open: gt, lt
  Comparator #(.width(6)) comparator_16 (.a(FunCode), .b(6'b011011), .eq(comparator_16_eq));  // open: gt, lt
  Comparator #(.width(6)) comparator_17 (.a(FunCode), .b(6'b010000), .eq(comparator_17_eq));  // open: gt, lt
  Comparator #(.width(6)) comparator_18 (.a(FunCode), .b(6'b010010), .eq(comparator_18_eq));  // open: gt, lt
  Comparator #(.width(6)) comparator_19 (.a(FunCode), .b({6{1'b0}}), .eq(comparator_19_eq));  // open: gt, lt
  Comparator #(.width(6)) comparator_20 (.a(FunCode), .b(6'b001000), .eq(comparator_20_eq));  // open: gt, lt
  Multiplexer #(.disabled(0), .enable("false")) multiplexer_1 (
    .in0(1'b0), .in1(comparator_21_eq), .out(multiplexer_1_out), .sel(Rs0));
  Comparator #(.width(6)) comparator_21 (.a(FunCode), .b({6{1'b0}}), .eq(comparator_21_eq));  // open: gt, lt
  Multiplexer #(.disabled(0), .enable("false")) multiplexer_2 (
    .in0(1'b0), .in1(comparator_22_eq), .out(multiplexer_2_out), .sel(Rs0));
  Comparator #(.width(6)) comparator_22 (.a(FunCode), .b(6'b000001), .eq(comparator_22_eq));  // open: gt, lt
  Multiplexer #(.disabled(0), .enable("false")) multiplexer_3 (
    .in0(1'b0), .in1(comparator_23_eq), .out(multiplexer_3_out), .sel(Rs1));
  Comparator #(.width(6)) comparator_23 (.a(FunCode), .b({6{1'b1}}), .eq(comparator_23_eq));  // open: gt, lt
  Multiplexer #(.disabled(0), .enable("false")) multiplexer_4 (
    .in0(1'b0), .in1(comparator_24_eq), .out(multiplexer_4_out), .sel(Rs1));
  Comparator #(.width(6)) comparator_24 (.a(FunCode), .b(6'b000010), .eq(comparator_24_eq));  // open: gt, lt
  Multiplexer #(.disabled(0), .enable("false")) multiplexer_5 (
    .in0(1'b0), .in1(comparator_25_eq), .out(multiplexer_5_out), .sel(Rs1));
  Comparator #(.width(6)) comparator_25 (.a(FunCode), .b(6'b000100), .eq(comparator_25_eq));  // open: gt, lt
  Multiplexer #(.disabled(0), .enable("false")) multiplexer_6 (
    .in0(1'b0), .in1(comparator_26_eq), .out(multiplexer_6_out), .sel(Rs1));
  Comparator #(.width(6)) comparator_26 (.a(FunCode), .b(6'b000001), .eq(comparator_26_eq));  // open: gt, lt
  Priority_Encoder #(.select(4), .disabled(0)) priority_encoder_2 (
    .in0(comparator_5_eq), .in1(comparator_6_eq), .in2(comparator_7_eq), .in3(comparator_8_eq),
    .in4(comparator_9_eq), .in5(comparator_10_eq), .in6(comparator_11_eq), .in7(comparator_12_eq),
    .in8(comparator_13_eq), .in9(comparator_14_eq), .in10(comparator_15_eq), .in11(comparator_16_eq),
    .in12(comparator_17_eq), .in13(comparator_18_eq), .in14(comparator_19_eq), .in15(comparator_20_eq),
    .out(OpSRb), .gs(VRb), .en_in(Rb));  // open: en_out
  Priority_Encoder #(.select(4), .disabled(0)) priority_encoder_3 (
    .in0(multiplexer_1_out), .in1(multiplexer_2_out), .in2(multiplexer_3_out), .in3(multiplexer_4_out),
    .in4(multiplexer_5_out), .in5(multiplexer_6_out), .in6(1'b0), .in7(1'b0), .in8(1'b0), .in9(1'b0),
    .in10(1'b0), .in11(1'b0), .in12(1'b0), .in13(1'b0), .in14(1'b0), .in15(1'b0), .out(OpSRs), .gs(VRs),
    .en_in(Rs));  // open: en_out
  and and_1 (and_1_out, Rb, VRb);
  and and_2 (and_2_out, Rs, VRs);
  and and_3 (and_3_out, I, VI);
  or or_2 (Valid__1_if_the_OC_and_FC_belong_to_a_valid_operation, J, and_1_out, and_2_out, and_3_out);
  Comparator #(.width(6)) comparator_27 (.a(OpCode), .b(6'b001000), .eq(comparator_27_eq));  // open: gt, lt
  Comparator #(.width(6)) comparator_28 (.a(OpCode), .b(6'b001010), .eq(comparator_28_eq));  // open: gt, lt
  Comparator #(.width(6)) comparator_29 (.a(OpCode), .b(6'b001011), .eq(comparator_29_eq));  // open: gt, lt
  Comparator #(.width(6)) comparator_30 (.a(OpCode), .b(6'b001100), .eq(comparator_30_eq));  // open: gt, lt
  Comparator #(.width(6)) comparator_31 (.a(OpCode), .b(6'b001101), .eq(comparator_31_eq));  // open: gt, lt
  Comparator #(.width(6)) comparator_32 (.a(OpCode), .b(6'b001110), .eq(comparator_32_eq));  // open: gt, lt
  Comparator #(.width(6)) comparator_33 (.a(OpCode), .b(6'b000100), .eq(comparator_33_eq));  // open: gt, lt
  Comparator #(.width(6)) comparator_34 (.a(OpCode), .b(6'b000101), .eq(comparator_34_eq));  // open: gt, lt
  Comparator #(.width(6)) comparator_35 (.a(OpCode), .b(6'b000110), .eq(comparator_35_eq));  // open: gt, lt
  Comparator #(.width(6)) comparator_36 (.a(OpCode), .b(6'b000111), .eq(comparator_36_eq));  // open: gt, lt
  Comparator #(.width(6)) comparator_37 (.a(OpCode), .b(6'b000001), .eq(comparator_37_eq));  // open: gt, lt
  Comparator #(.width(6)) comparator_38 (.a(OpCode), .b(6'b100011), .eq(comparator_38_eq));  // open: gt, lt
  Comparator #(.width(6)) comparator_39 (.a(OpCode), .b(6'b101011), .eq(comparator_39_eq));  // open: gt, lt
  Pull_Resistor pull_resistor_1 (.node(OpSRb));
  Pull_Resistor pull_resistor_2 (.node(OpSRs));
  Pull_Resistor pull_resistor_3 (.node(OpSI));
  Pull_Resistor pull_resistor_4 (.node(OpSJ));
  assign OpS__Selector_of_the_operation = OpSRb | OpSRs | OpSI | OpSJ;  // OR_Gate or_3, 4 bits wide
  Priority_Encoder #(.select(4), .disabled(0)) priority_encoder_4 (
    .in0(comparator_27_eq), .in1(comparator_28_eq), .in2(comparator_29_eq), .in3(comparator_30_eq),
    .in4(comparator_31_eq), .in5(comparator_32_eq), .in6(comparator_33_eq), .in7(comparator_34_eq),
    .in8(comparator_35_eq), .in9(comparator_36_eq), .in10(comparator_37_eq), .in11(comparator_38_eq),
    .in12(comparator_39_eq), .in13(1'b0), .in14(1'b0), .in15(1'b0), .out(OpSI), .gs(VI), .en_in(I));  // open: en_out

  // Other names for the same wires on the sheet: FC[5:0] = FunCode; OC[5:0] = OpCode;
  //   OpS[3:0] = OpS__Selector_of_the_operation;
  //   Type[1:0] = Type__0_for_basic_type_R__and_1_for_special_R__2_for_type_I_and_3_for_type_J;
  //   Valid = Valid__1_if_the_OC_and_FC_belong_to_a_valid_operation
endmodule

module RbALUResult (
  input  Start,
  input  Clk,
  input  Rst,
  input  [3:0] SALU,
  output ER,
  output [1:0] SA,
  output [1:0] SB,
  output EB,
  output [3:0] SALU_2,
  output EALU,
  output [1:0] SW,
  output EW,
  output End
);

  Multiplexer #(.width(2), .disabled(0), .enable("false")) multiplexer_1 (
    .in0(2'b00), .in1(2'b01), .out(SA), .sel(Start));
  Multiplexer #(.width(2), .disabled(0), .enable("false")) multiplexer_2 (
    .in0(2'b00), .in1(2'b01), .out(SB), .sel(Start));
  Multiplexer #(.width(4), .disabled(0), .enable("false")) multiplexer_3 (
    .in0(4'b0000), .in1(SALU), .out(SALU_2), .sel(Start));

  assign EALU = Start;
  assign EB = Start;
  assign End = Start;
  assign ER = Start;
  assign EW = Start;
  assign SW = 2'b00;

  // Other names for the same wires on the sheet: St = Start

  // Notes on the sheet:
  //   Input
  //   Ground
  //   Output
endmodule

module RbALULoHi (
  input  Start,
  input  Clk,
  input  Rst,
  input  [3:0] SALU,
  output [1:0] SA,
  output [1:0] SB,
  output EB,
  output ER,
  output [3:0] SALU_2,
  output EALU,
  output EHi,
  output ELo,
  output End
);

  Multiplexer #(.width(2), .disabled(0), .enable("false")) multiplexer_1 (
    .in0(2'b00), .in1(2'b01), .out(SA), .sel(Start));
  Multiplexer #(.width(2), .disabled(0), .enable("false")) multiplexer_2 (
    .in0(2'b00), .in1(2'b01), .out(SB), .sel(Start));
  Multiplexer #(.width(4), .disabled(0), .enable("false")) multiplexer_3 (
    .in0(4'b0000), .in1(SALU), .out(SALU_2), .sel(Start));

  assign EALU = Start;
  assign EB = Start;
  assign EHi = Start;
  assign ELo = Start;
  assign End = Start;
  assign ER = Start;

  // Other names for the same wires on the sheet: St = Start

  // Notes on the sheet:
  //   Input
  //   Ground
  //   Output
endmodule

module nop (
  input  Start,
  input  Clk,
  input  Rst,
  output [1:0] SA,
  output [1:0] SB,
  output EB,
  output [3:0] SALU,
  output EPC,
  output End
);


  assign EB = Start;
  assign End = Start;
  assign EPC = Start;
  assign SA = 2'b00;
  assign SALU = 4'b0000;
  assign SB = 2'b00;

  // Other names for the same wires on the sheet: St = Start

  // Notes on the sheet:
  //   Input
  //   Ground
  //   Output
endmodule

module j (
  input  Start,
  input  Clk,
  input  Rst,
  output [1:0] SA,
  output [1:0] SB,
  output EB,
  output [3:0] SALU,
  output EPC,
  output End
);

  Multiplexer #(.width(2), .disabled(0), .enable("false")) multiplexer_1 (
    .in0(2'b00), .in1(2'b10), .out(SA), .sel(Start));

  assign EB = 1'b0;
  assign End = Start;
  assign EPC = Start;
  assign SALU = 4'b0000;
  assign SB = 2'b00;

  // Other names for the same wires on the sheet: St = Start

  // Notes on the sheet:
  //   Input
  //   Ground
  //   Output
endmodule

module jr (
  input  Start,
  input  Clk,
  input  Rst,
  output [1:0] SA,
  output [1:0] SB,
  output EB,
  output ER,
  output [3:0] SALU,
  output EPC,
  output End
);

  Multiplexer #(.width(2), .disabled(0), .enable("false")) multiplexer_1 (
    .in0(2'b00), .in1(2'b01), .out(SA), .sel(Start));

  assign EB = 1'b0;
  assign End = Start;
  assign EPC = Start;
  assign ER = Start;
  assign SALU = 4'b0000;
  assign SB = 2'b00;

  // Other names for the same wires on the sheet: St = Start

  // Notes on the sheet:
  //   Input
  //   Ground
  //   Output
endmodule

module IALU (
  input  Start,
  input  Clk,
  input  Rst,
  input  [3:0] SALU,
  output ER,
  output [1:0] SA,
  output [1:0] SB,
  output EB,
  output SWA,
  output SIS,
  output [3:0] SALU_2,
  output EALU,
  output [1:0] SW,
  output EW,
  output End
);

  wire comparator_1_lt;
  wire [3:0] SALU_t;

  Multiplexer #(.select(3), .width(4), .disabled(0), .enable("false")) multiplexer_1 (
    .in0(4'b0000), .in1(4'b0110), .in2(4'b0111), .in3(4'b0010), .in4(4'b0011), .in5(4'b0101), .in6(4'b0000),
    .in7(4'b0000), .out(SALU_t), .sel(SALU[2:0]));
  Comparator #(.width(4), .mode("unsigned")) comparator_1 (
    .a(4'b0010), .b(SALU), .lt(comparator_1_lt));  // open: gt, eq
  Multiplexer #(.width(2), .disabled(0), .enable("false")) multiplexer_2 (
    .in0(2'b00), .in1(2'b01), .out(SA), .sel(Start));
  Multiplexer #(.width(2), .disabled(0), .enable("false")) multiplexer_3 (
    .in0(2'b00), .in1(2'b10), .out(SB), .sel(Start));
  and and_1 (SIS, comparator_1_lt, Start);
  Multiplexer #(.width(4), .disabled(0), .enable("false")) multiplexer_4 (
    .in0(4'b0000), .in1(SALU_t), .out(SALU_2), .sel(Start));

  assign EALU = Start;
  assign EB = Start;
  assign End = Start;
  assign ER = Start;
  assign EW = Start;
  assign SW = 2'b00;
  assign SWA = Start;

  // Other names for the same wires on the sheet: OS[3:0] = SALU; St = Start

  // Notes on the sheet:
  //   Input
  //   Ground
  //   Output
endmodule

module Ibf (
  input  Start,
  input  Clk,
  input  Rst,
  input  [3:0] OS,
  input  ZF,
  input  NF,
  output ER,
  output [1:0] SA,
  output [1:0] SB,
  output EB,
  output [3:0] SALU,
  output EALU,
  output EPC,
  output End
);

  wire and_1_out, comparator_1_lt, comparator_2_eq, comparator_3_eq, comparator_4_eq, comparator_5_eq,
       comparator_6_eq, decoder_1_out1, End0, ISI4, not_1_out, not_2_out, or_3_out;
  wire [1:0] multiplexer_2_out;
  wire [2:0] S;

  Comparator #(.width(3), .mode("unsigned")) comparator_1 (.a(S), .b(3'b010), .lt(comparator_1_lt));  // open: gt, eq
  Multiplexer #(.width(2), .disabled(0), .enable("false")) multiplexer_1 (
    .in0(2'b00), .in1(2'b01), .out(SA), .sel(Start));
  Multiplexer #(.width(2), .disabled(0), .enable("false")) multiplexer_2 (
    .in0(2'b00), .in1(2'b01), .out(multiplexer_2_out), .sel(Start));
  and and_1 (and_1_out, Start, comparator_1_lt);
  or or_1 (EB, and_1_out, EPC);
  Multiplexer #(.width(4), .disabled(0), .enable("false")) multiplexer_3 (
    .in0(4'b0000), .in1(4'b0001), .out(SALU), .sel(Start));
  or or_2 (End, End0, EPC);
  Multiplexer #(.width(2), .disabled(0), .enable("false")) multiplexer_4 (
    .in0(multiplexer_2_out), .in1(2'b11), .out(SB), .sel(EPC));
  Comparator #(.width(4), .mode("unsigned")) comparator_2 (.a(OS), .b(4'b0110), .eq(comparator_2_eq));  // open: gt, lt
  Comparator #(.width(4), .mode("unsigned")) comparator_3 (.a(OS), .b(4'b0111), .eq(comparator_3_eq));  // open: gt, lt
  Comparator #(.width(4), .mode("unsigned")) comparator_4 (.a(OS), .b(4'b1000), .eq(comparator_4_eq));  // open: gt, lt
  Comparator #(.width(4), .mode("unsigned")) comparator_5 (.a(OS), .b(4'b1001), .eq(comparator_5_eq));  // open: gt, lt
  Comparator #(.width(4), .mode("unsigned")) comparator_6 (.a(OS), .b(4'b1010), .eq(comparator_6_eq));  // open: gt, lt
  not not_1 (not_1_out, ZF);
  or or_3 (or_3_out, ZF, NF);
  not not_2 (not_2_out, or_3_out);
  Priority_Encoder #(.disabled(0)) priority_encoder_1 (
    .in0(comparator_2_eq), .in1(comparator_3_eq), .in2(comparator_4_eq), .in3(comparator_5_eq),
    .in4(comparator_6_eq), .in5(1'b0), .in6(1'b0), .in7(1'b0), .out(S));  // open: en_in, gs, en_out
  Pull_Resistor pull_resistor_1 (.node(S));
  Multiplexer #(.select(3), .disabled(0), .enable("false")) multiplexer_5 (
    .in0(ZF), .in1(not_1_out), .in2(or_3_out), .in3(not_2_out), .in4(NF), .in5(1'b0), .in6(1'b0), .in7(1'b0),
    .out(ISI4), .sel(S));
  Decoder #(.disabled(0)) decoder_1 (.out0(End0), .out1(decoder_1_out1), .sel(ISI4), .en(Start));
  D_Flip_Flop u_ISI4 (.clk(Clk), .D(decoder_1_out1), .Q(EPC), .reset(Rst));  // open: Qn, preset, en

  assign EALU = Start;
  assign ER = Start;

  // Other names for the same wires on the sheet: IS = EPC; St = Start

  // Notes on the sheet:
  //   Input
  //   Ground
  //   Output
  //   Check Operation
  //   Check Conditions
  //   New State
endmodule

module RbMfhi_lo (
  input  Start,
  input  Clk,
  input  Rst,
  input  [3:0] SOp,
  output [1:0] SW,
  output EW,
  output End
);

  wire [1:0] SW_t;

  Multiplexer #(.width(2), .enable("false")) multiplexer_1 (.in0(2'b11), .in1(2'b10), .out(SW_t), .sel(SOp[0]));
  Multiplexer #(.width(2), .disabled(0), .enable("false")) multiplexer_2 (
    .in0(2'b00), .in1(SW_t), .out(SW), .sel(Start));

  assign End = Start;
  assign EW = Start;

  // Other names for the same wires on the sheet: St = Start

  // Notes on the sheet:
  //   Input
  //   Selector
  //   Output
endmodule

module lw_sw (
  input  Start,
  input  Clk,
  input  Rst,
  input  [3:0] SALU,
  input  Busy,
  output ER,
  output [1:0] SA,
  output [1:0] SB,
  output EB,
  output SIS,
  output [3:0] SALU_2,
  output EALU,
  output IorDS,
  output SD,
  output CS,
  output R_W,
  output EMDR,
  output SMR,
  output [1:0] SW3,
  output SWA,
  output EW,
  output End
);

  wire demultiplexer_1_out0, demultiplexer_1_out1, demultiplexer_2_out0, demultiplexer_2_out1, not_1_out,
       or_2_out, WaitingRam_q;

  Multiplexer #(.width(2), .disabled(0), .enable("false")) multiplexer_1 (.in0(2'b00), .in1(2'b01), .out(SA), .sel(CS));
  Multiplexer #(.width(2), .disabled(0), .enable("false")) multiplexer_2 (.in0(2'b00), .in1(2'b10), .out(SB), .sel(CS));
  Multiplexer #(.disabled(0), .enable("false")) multiplexer_3 (.in0(1'b0), .in1(not_1_out), .out(R_W), .sel(CS));
  not not_1 (not_1_out, SALU[0]);
  Multiplexer #(.disabled(0), .enable("false")) multiplexer_4 (.in0(1'b0), .in1(SALU[0]), .out(EMDR), .sel(End));
  Multiplexer #(.width(2), .disabled(0), .enable("false")) multiplexer_5 (
    .in0(2'b00), .in1(2'b01), .out(SW3), .sel(End));
  Multiplexer #(.disabled(0), .enable("false")) multiplexer_6 (.in0(1'b0), .in1(SALU[0]), .out(SWA), .sel(End));
  Multiplexer #(.disabled(0), .enable("false")) multiplexer_7 (.in0(1'b0), .in1(SALU[0]), .out(EW), .sel(End));
  Demultiplexer #(.disabled(0), .enable("false")) demultiplexer_1 (
    .out0(demultiplexer_1_out0), .out1(demultiplexer_1_out1), .in(Start), .sel(Busy));
  or or_1 (CS, Start, or_2_out);
  or or_2 (or_2_out, demultiplexer_1_out1, demultiplexer_2_out1);
  D_Flip_Flop WaitingRam (.clk(Clk), .D(or_2_out), .Q(WaitingRam_q), .reset(Rst));  // open: Qn, preset, en
  Demultiplexer #(.disabled(0), .enable("false")) demultiplexer_2 (
    .out0(demultiplexer_2_out0), .out1(demultiplexer_2_out1), .in(WaitingRam_q), .sel(Busy));
  or or_3 (End, demultiplexer_1_out0, demultiplexer_2_out0);

  assign EALU = CS;
  assign EB = CS;
  assign ER = CS;
  assign IorDS = CS;
  assign SALU_2 = 4'b0000;
  assign SD = CS;
  assign SIS = 1'b0;
  assign SMR = 1'b0;

  // Other names for the same wires on the sheet: Ready = End; _0p = SALU[0]; St = CS

  // Notes on the sheet:
  //   Input
  //   Ground
  //   Output
  //   Circuit
endmodule

module RsPop (
  input  Start,
  input  Clk,
  input  Rst,
  input  Busy,
  output ER,
  output SSPR,
  output [1:0] SA,
  output [1:0] SB,
  output EB,
  output [3:0] SALU,
  output IorDS,
  output SD,
  output CS,
  output R_W,
  output EMDR,
  output SMR,
  output [1:0] SW3,
  output SWA,
  output EW,
  output SSPW,
  output End
);

  wire demultiplexer_1_out0, demultiplexer_1_out1, demultiplexer_2_out0, demultiplexer_2_out1, or_3_out,
       or_6_out, WaitingRam_q;

  or or_1 (ER, CS, End);
  or or_2 (SSPR, CS, End);
  Multiplexer #(.width(2), .disabled(0), .enable("false")) multiplexer_1 (
    .in0(2'b00), .in1(2'b01), .out(SA), .sel(or_3_out));
  or or_3 (or_3_out, CS, End);
  Multiplexer #(.disabled(0), .enable("false")) multiplexer_2 (.in0(1'b0), .in1(1'b1), .out(EB), .sel(End));
  Multiplexer #(.width(2), .disabled(0), .enable("false")) multiplexer_3 (
    .in0(2'b00), .in1(2'b01), .out(SW3), .sel(EMDR));
  or or_4 (EW, EMDR, End);
  Demultiplexer #(.disabled(0), .enable("false")) demultiplexer_1 (
    .out0(demultiplexer_1_out0), .out1(demultiplexer_1_out1), .in(Start), .sel(Busy));
  or or_5 (CS, Start, or_6_out);
  or or_6 (or_6_out, demultiplexer_1_out1, demultiplexer_2_out1);
  D_Flip_Flop WaitingRam (.clk(Clk), .D(or_6_out), .Q(WaitingRam_q), .reset(Rst));  // open: Qn, preset, en
  Demultiplexer #(.disabled(0), .enable("false")) demultiplexer_2 (
    .out0(demultiplexer_2_out0), .out1(demultiplexer_2_out1), .in(WaitingRam_q), .sel(Busy));
  or or_7 (EMDR, demultiplexer_1_out0, demultiplexer_2_out0);
  D_Flip_Flop SP (.clk(Clk), .D(EMDR), .Q(End), .reset(Rst));  // open: Qn, preset, en

  assign IorDS = CS;
  assign R_W = 1'b0;
  assign SALU = 4'b0000;
  assign SB = 2'b00;
  assign SD = 1'b0;
  assign SMR = 1'b0;
  assign SSPW = End;
  assign SWA = 1'b0;

  // Other names for the same wires on the sheet: Ready = EMDR; St = CS

  // Notes on the sheet:
  //   Input
  //   Ground
  //   Output
  //   Circuit
endmodule

module RsPush (
  input  Start,
  input  Clk,
  input  Rst,
  input  Busy,
  output ER,
  output SSPR,
  output [1:0] SA,
  output [1:0] SB,
  output EB,
  output [3:0] SALU,
  output SSPW,
  output [1:0] SW3,
  output SWA,
  output SPDir,
  output EW,
  output IorDS,
  output SD,
  output CS,
  output R_W,
  output End
);

  wire demultiplexer_1_out0, demultiplexer_1_out1, demultiplexer_2_out0, demultiplexer_2_out1, or_2_out,
       or_5_out, SP_q, WaitingRam_q;

  or or_1 (ER, Start, CS);
  Multiplexer #(.width(2), .disabled(0), .enable("false")) multiplexer_1 (
    .in0(2'b00), .in1(2'b01), .out(SA), .sel(or_2_out));
  or or_2 (or_2_out, Start, End);
  Multiplexer #(.disabled(0), .enable("false")) multiplexer_2 (.in0(1'b0), .in1(1'b1), .out(EB), .sel(Start));
  Multiplexer #(.width(4), .disabled(0), .enable("false")) multiplexer_3 (
    .in0(4'b0000), .in1(4'b0001), .out(SALU), .sel(Start));
  or or_3 (SSPW, Start, CS);
  Multiplexer #(.disabled(0), .enable("false")) multiplexer_4 (.in0(1'b0), .in1(1'b1), .out(R_W), .sel(CS));
  D_Flip_Flop SP (.clk(Clk), .D(Start), .Q(SP_q), .reset(Rst));  // open: Qn, preset, en
  Demultiplexer #(.disabled(0), .enable("false")) demultiplexer_1 (
    .out0(demultiplexer_1_out0), .out1(demultiplexer_1_out1), .in(SP_q), .sel(Busy));
  or or_4 (CS, SP_q, or_5_out);
  or or_5 (or_5_out, demultiplexer_1_out1, demultiplexer_2_out1);
  D_Flip_Flop WaitingRam (.clk(Clk), .D(or_5_out), .Q(WaitingRam_q), .reset(Rst));  // open: Qn, preset, en
  Demultiplexer #(.disabled(0), .enable("false")) demultiplexer_2 (
    .out0(demultiplexer_2_out0), .out1(demultiplexer_2_out1), .in(WaitingRam_q), .sel(Busy));
  or or_6 (End, demultiplexer_1_out0, demultiplexer_2_out0);

  assign EW = Start;
  assign IorDS = CS;
  assign SB = 2'b00;
  assign SD = 1'b0;
  assign SPDir = CS;
  assign SSPR = Start;
  assign SW3 = 2'b00;
  assign SWA = 1'b0;

  // Other names for the same wires on the sheet: Write = CS

  // Notes on the sheet:
  //   Input
  //   Ground
  //   Output
  //   Circuit
endmodule

module RsTty (
  input  Start,
  output ETty,
  output ER,
  output End
);


  assign End = Start;
  assign ER = Start;
  assign ETty = Start;
endmodule

module RsRnd (
  input  Start,
  input  Clk,
  input  Rst,
  output SMR,
  output [1:0] SW3,
  output EW,
  output End
);

  Multiplexer #(.width(2), .disabled(0), .enable("false")) multiplexer_1 (
    .in0(2'b00), .in1(2'b01), .out(SW3), .sel(Start));

  assign End = Start;
  assign EW = Start;
  assign SMR = Start;

  // Other names for the same wires on the sheet: St = Start

  // Notes on the sheet:
  //   Input
  //   Ground
  //   Output
endmodule

module RsKbd (
  input  Start,
  output EW,
  output EKBD,
  output End
);


  assign EKBD = Start;
  assign End = Start;
  assign EW = Start;

  // Notes on the sheet:
  //   Input
  //   Output
endmodule
