// Logisim project DataPath.circ as structural Verilog: 2 circuits, main circuit -DataPath-
module DataPath (
  input  EPC,
  input  [15:0] Const16,
  input  [31:0] IRD__Data_to_write_IR__Instruction_Register,
  input  [25:0] Const26,
  input  EIR,
  input  ER__Enable_Reading,
  input  [4:0] A1__Direction_of_first_register_to_read,
  input  [31:0] MDRD__Data_to_write_MDR__Memory_Data_Register,
  input  [4:0] A2__Direction_of_second_register_to_read,
  input  EMDR,
  input  [4:0] A3__Direction_of_register_to_write,
  input  EALUOut,
  input  [1:0] SW3__Selector_to_Write_Register_0_to_write_output_of_ALU__1_to_write_from_Memory__2_to_write_from_Lo_and_3_to_write_from_Hi,
  input  EHi,
  input  EW__Enable_Writing,
  input  ELo,
  input  SSPR__When_1__A1_points_to_SP,
  input  SD__0_to_output_A_to_Data_and_1_to_output_B,
  input  SSPW__When_1__A3_points_to_SP,
  input  IorDS__Selector_of_Dir_output__0_returns_PC__1_returns_ALUOut,
  input  [3:0] SALU__Op_Selector_of_ALU,
  input  SWA__When_0_writes_in_dir_A3__when_1_writes_in_dir_A2,
  input  [1:0] SSrcA__Selector_of_SrcA_output__0_returns_PC__1_returns_A__2_returns_jPC_and_3_returns_PC_ISd4,
  input  SMR__When_0_MD_from_SW3_returns_MD_and_when_1_returns_a_random_number,
  input  [1:0] SSrcB__Selector_of_SrcB_output__0_returns_4__1_returns_B__2_returns_IS_and_3_returns_ISd4,
  input  SIS__Selector_of_type_of_constant__when_0_const_is_used_as_I15Const__when_1_it_s_0Const,
  input  ESrcB__When_0_SrcB_returns_0,
  input  Akbd,
  input  [6:0] Dkbd,
  input  Ekbd,
  input  Clk,
  input  Rst,
  output [31:0] PC,
  output [31:0] IR,
  output [31:0] MDR,
  output [31:0] Data,
  output [31:0] ALU,
  output [31:0] Hi,
  output [31:0] Lo,
  output [31:0] A,
  output [31:0] B,
  output [31:0] DIR,
  output [6:0] tty,
  output ZF,
  output NF
);

  wire NFD, NFOut, ZFD, ZFOut;
  wire [4:0] multiplexer_12_out, multiplexer_17_out;
  wire [31:0] _0Const, AD, ALUD, ALUOut, ALUSrcA, ALUSrcB, BD, bit_extender_1_out, HiOut, I15Const, IS, ISd4,
       kbd, MD, multiplexer_7_out, multiplexer_8_out, multiplexer_9_out, multiplexer_13_out,
       multiplexer_14_out, multiplexer_18_out, multiplexer_19_out, Rd, WD3;
  wire [31:7] multiplexer_2_out;

  Pull_Resistor pull_resistor_1 (.node(ZF));
  Pull_Resistor pull_resistor_2 (.node(NF));
  Multiplexer #(.enable("false")) multiplexer_1 (.in0(ZFD), .in1(ZFOut), .out(ZF), .sel(EALUOut));
  ALU alu_1 (
    .A(ALUSrcA), .B(ALUSrcB), .ALU_Control(SALU__Op_Selector_of_ALU), .Result(ALUOut), .Zero_Flag(ZFOut),
    .Hi(HiOut), .Negative_Flag(NFOut));
  Multiplexer #(.width(32), .enable("false")) multiplexer_2 (
    .in0(A), .in1(AD), .out({multiplexer_2_out, tty}), .sel(ER__Enable_Reading));
  Multiplexer #(.enable("false")) multiplexer_3 (.in0(NFD), .in1(NFOut), .out(NF), .sel(EALUOut));
  Multiplexer #(.width(32), .enable("false")) multiplexer_4 (
    .in0(MDR), .in1(MDRD__Data_to_write_MDR__Memory_Data_Register), .out(MD), .sel(EMDR));
  Multiplexer #(.width(32), .enable("false")) multiplexer_5 (
    .in0({32{1'b1}}), .in1(bit_extender_1_out), .out(kbd), .sel(Akbd));
  assign bit_extender_1_out = {{25{1'b0}}, Dkbd};  // Bit_Extender bit_extender_1
  Multiplexer #(.width(32), .enable("false")) multiplexer_6 (.in0(ALUD), .in1(ALUOut), .out(ALU), .sel(EALUOut));
  Multiplexer #(.width(32), .disabled(0), .enable("false")) multiplexer_7 (
    .in0(MD), .in1(Rd), .out(multiplexer_7_out),
    .sel(SMR__When_0_MD_from_SW3_returns_MD_and_when_1_returns_a_random_number));
  Multiplexer #(.width(32), .enable("false")) multiplexer_8 (
    .in0(A), .in1(AD), .out(multiplexer_8_out), .sel(ER__Enable_Reading));
  Multiplexer #(.width(32), .enable("false")) multiplexer_9 (
    .in0(B), .in1(BD), .out(multiplexer_9_out), .sel(ER__Enable_Reading));
  Multiplexer #(.select(2), .width(32), .enable("false")) multiplexer_10 (
    .in0(ALU), .in1(multiplexer_7_out), .in2(Lo), .in3(Hi), .out(WD3),
    .sel(SW3__Selector_to_Write_Register_0_to_write_output_of_ALU__1_to_write_from_Memory__2_to_write_from_Lo_and_3_to_write_from_Hi));
  Multiplexer #(.width(32), .enable("false")) multiplexer_11 (
    .in0(multiplexer_8_out), .in1(multiplexer_9_out), .out(Data),
    .sel(SD__0_to_output_A_to_Data_and_1_to_output_B));
  Multiplexer #(.width(5), .disabled(0), .enable("false")) multiplexer_12 (
    .in0(A3__Direction_of_register_to_write), .in1(A2__Direction_of_second_register_to_read),
    .out(multiplexer_12_out), .sel(SWA__When_0_writes_in_dir_A3__when_1_writes_in_dir_A2));
  Multiplexer #(.width(32), .enable("false")) multiplexer_13 (
    .in0(WD3), .in1(kbd), .out(multiplexer_13_out), .sel(Ekbd));
  Multiplexer #(.width(32), .enable("false")) multiplexer_14 (
    .in0(multiplexer_13_out), .in1(ALUOut), .out(multiplexer_14_out), .sel(SSPW__When_1__A3_points_to_SP));
  Multiplexer #(.width(32), .enable("false")) multiplexer_15 (
    .in0(PC), .in1(ALUOut), .out(DIR), .sel(IorDS__Selector_of_Dir_output__0_returns_PC__1_returns_ALUOut));
  Multiplexer #(.width(32), .enable("false")) multiplexer_16 (
    .in0(I15Const), .in1(_0Const), .out(IS),
    .sel(SIS__Selector_of_type_of_constant__when_0_const_is_used_as_I15Const__when_1_it_s_0Const));
  Random #(.width(32)) random_1 (.clk(Clk), .out(Rd));  // open: next, clr
  assign _0Const = {{16{1'b0}}, Const16};  // Bit_Extender bit_extender_2
  Register #(.width(32), .trigger("falling")) u_PC (.D(ALUOut), .en(EPC), .Q(PC), .clk(Clk), .clr(Rst));
  Register #(.width(32), .trigger("falling")) u_MDR (
    .D(MDRD__Data_to_write_MDR__Memory_Data_Register), .en(EMDR), .Q(MDR), .clk(Clk), .clr(Rst));
  Register #(.width(32), .trigger("falling")) u_Hi (.D(HiOut), .en(EHi), .Q(Hi), .clk(Clk), .clr(Rst));
  Register #(.width(32), .trigger("falling")) u_A (.D(AD), .en(ER__Enable_Reading), .Q(A), .clk(Clk), .clr(Rst));
  Register #(.width(1), .trigger("falling")) u_ZF (.D(ZFOut), .en(EALUOut), .Q(ZFD), .clk(Clk), .clr(Rst));
  Multiplexer #(.width(5), .disabled(0), .enable("false")) multiplexer_17 (
    .in0(A1__Direction_of_first_register_to_read), .in1({5{1'b1}}), .out(multiplexer_17_out),
    .sel(SSPR__When_1__A1_points_to_SP));
  Register_File register_file_1 (
    .Clk__Detects_changes_in_the_clock(Clk), .A1__Address_of_the_first_register_to_read(multiplexer_17_out),
    .A2__Address_of_the_second_register_to_read(A2__Direction_of_second_register_to_read),
    .A3__Addres_of_the_third_register_to_write(multiplexer_12_out),
    .WD3__Data_to_write_in_the_register_of_address_A3(multiplexer_14_out),
    .WE3__Enable_Disable_writing(EW__Enable_Writing), .Rst__Reset_every_register_to_0(Rst),
    .RD1___Output__First_data_read(AD), .RD2___Output__Second_data_read(BD),
    .SSPW__When_1__A3_is_ignored_and_points_to_R31__R31_is_only_modified_if_SSP_is_enable(SSPW__When_1__A3_points_to_SP));
  Multiplexer #(.width(32), .enable("false")) multiplexer_18 (
    .in0(A), .in1(AD), .out(multiplexer_18_out), .sel(ER__Enable_Reading));
  Multiplexer #(.width(32), .enable("false")) multiplexer_19 (
    .in0(B), .in1(BD), .out(multiplexer_19_out), .sel(ER__Enable_Reading));
  assign I15Const = {{16{Const16[15]}}, Const16};  // Bit_Extender bit_extender_3
  Shifter #(.width(32)) shifter_1 (.in(IS), .\dist (5'b00010), .out(ISd4));
  Register #(.width(32), .trigger("falling")) u_IR (
    .D(IRD__Data_to_write_IR__Instruction_Register), .en(EIR), .Q(IR), .clk(Clk), .clr(Rst));
  Register #(.width(32), .trigger("falling")) u_ALUOut (.D(ALUOut), .en(EALUOut), .Q(ALUD), .clk(Clk), .clr(Rst));
  Register #(.width(32), .trigger("falling")) u_Lo (.D(ALUOut), .en(ELo), .Q(Lo), .clk(Clk), .clr(Rst));
  Register #(.width(32), .trigger("falling")) u_B (.D(BD), .en(ER__Enable_Reading), .Q(B), .clk(Clk), .clr(Rst));
  Register #(.width(1), .trigger("falling")) u_NF (.D(NFOut), .en(EALUOut), .Q(NFD), .clk(Clk), .clr(Rst));
  Multiplexer #(.select(2), .width(32), .enable("false")) multiplexer_20 (
    .in0(PC), .in1(multiplexer_18_out), .in2({PC[31:28], Const26, 2'b00}), .in3({32{1'b0}}), .out(ALUSrcA),
    .sel(SSrcA__Selector_of_SrcA_output__0_returns_PC__1_returns_A__2_returns_jPC_and_3_returns_PC_ISd4));
  Multiplexer #(.select(2), .width(32), .disabled(0)) multiplexer_21 (
    .in0(32'h4), .in1(multiplexer_19_out), .in2(IS), .in3(ISd4), .out(ALUSrcB),
    .sel(SSrcB__Selector_of_SrcB_output__0_returns_4__1_returns_B__2_returns_IS_and_3_returns_ISd4),
    .en(ESrcB__When_0_SrcB_returns_0));

  // Other names for the same wires on the sheet: A1[4:0] = A1__Direction_of_first_register_to_read;
  //   A2[4:0] = A2__Direction_of_second_register_to_read; A3[4:0] = A3__Direction_of_register_to_write;
  //   ER = ER__Enable_Reading; ESrcB = ESrcB__When_0_SrcB_returns_0; EW = EW__Enable_Writing;
  //   IorDS = IorDS__Selector_of_Dir_output__0_returns_PC__1_returns_ALUOut;
  //   IRD[31:0] = IRD__Data_to_write_IR__Instruction_Register; jPC[31:2] = {PC[31:28], Const26};
  //   MDRD[31:0] = MDRD__Data_to_write_MDR__Memory_Data_Register; SALU[3:0] = SALU__Op_Selector_of_ALU;
  //   SD = SD__0_to_output_A_to_Data_and_1_to_output_B;
  //   SIS = SIS__Selector_of_type_of_constant__when_0_const_is_used_as_I15Const__when_1_it_s_0Const;
  //   SMR = SMR__When_0_MD_from_SW3_returns_MD_and_when_1_returns_a_random_number;
  //   SSPR = SSPR__When_1__A1_points_to_SP; SSPW = SSPW__When_1__A3_points_to_SP;
  //   SSrcA[1:0] = SSrcA__Selector_of_SrcA_output__0_returns_PC__1_returns_A__2_returns_jPC_and_3_returns_PC_ISd4;
  //   SSrcB[1:0] = SSrcB__Selector_of_SrcB_output__0_returns_4__1_returns_B__2_returns_IS_and_3_returns_ISd4;
  //   SW3[1:0] = SW3__Selector_to_Write_Register_0_to_write_output_of_ALU__1_to_write_from_Memory__2_to_write_from_Lo_and_3_to_write_from_Hi;
  //   SWA = SWA__When_0_writes_in_dir_A3__when_1_writes_in_dir_A2

  // Notes on the sheet:
  //   Input
  //   Output
  //   Registers
  //   Multiplexers and Operations
endmodule

module Register_File (
  input  Clk__Detects_changes_in_the_clock,
  input  [4:0] A1__Address_of_the_first_register_to_read,
  input  [4:0] A2__Address_of_the_second_register_to_read,
  input  SSPW__When_1__A3_is_ignored_and_points_to_R31__R31_is_only_modified_if_SSP_is_enable,
  input  [4:0] A3__Addres_of_the_third_register_to_write,
  input  [31:0] WD3__Data_to_write_in_the_register_of_address_A3,
  input  WE3__Enable_Disable_writing,
  input  Rst__Reset_every_register_to_0,
  output [31:0] RD1___Output__First_data_read,
  output [31:0] RD2___Output__Second_data_read
);

  wire and_1_out, and_2_out, E0, E1, E2, E3, E4, E5, E6, E7, E8, E9, E10, E11, E12, E13, E14, E15, E16, E17,
       E18, E19, E20, E21, E22, E23, E24, E25, E26, E27, E28, E29, E30, E31, not_1_out;
  wire [31:0] R0, R1, R2, R3, R4, R5, R6, R7, R8, R9, R10, R11, R12, R13, R14, R15, R16, R17, R18, R19, R20,
       R21, R22, R23, R24, R25, R26, R27, R28, R29, R30, SP;

  Register #(.width(32), .trigger("falling")) u_R0 (
    .D({32{1'b0}}), .en(E0), .Q(R0), .clk(Clk__Detects_changes_in_the_clock),
    .clr(Rst__Reset_every_register_to_0));
  Register #(.width(32), .trigger("falling")) u_R2 (
    .D(WD3__Data_to_write_in_the_register_of_address_A3), .en(E2), .Q(R2),
    .clk(Clk__Detects_changes_in_the_clock), .clr(Rst__Reset_every_register_to_0));
  Register #(.width(32), .trigger("falling")) u_R4 (
    .D(WD3__Data_to_write_in_the_register_of_address_A3), .en(E4), .Q(R4),
    .clk(Clk__Detects_changes_in_the_clock), .clr(Rst__Reset_every_register_to_0));
  Register #(.width(32), .trigger("falling")) u_R6 (
    .D(WD3__Data_to_write_in_the_register_of_address_A3), .en(E6), .Q(R6),
    .clk(Clk__Detects_changes_in_the_clock), .clr(Rst__Reset_every_register_to_0));
  Register #(.width(32), .trigger("falling")) u_R8 (
    .D(WD3__Data_to_write_in_the_register_of_address_A3), .en(E8), .Q(R8),
    .clk(Clk__Detects_changes_in_the_clock), .clr(Rst__Reset_every_register_to_0));
  Register #(.width(32), .trigger("falling")) u_R10 (
    .D(WD3__Data_to_write_in_the_register_of_address_A3), .en(E10), .Q(R10),
    .clk(Clk__Detects_changes_in_the_clock), .clr(Rst__Reset_every_register_to_0));
  Register #(.width(32), .trigger("falling")) u_R12 (
    .D(WD3__Data_to_write_in_the_register_of_address_A3), .en(E12), .Q(R12),
    .clk(Clk__Detects_changes_in_the_clock), .clr(Rst__Reset_every_register_to_0));
  Register #(.width(32), .trigger("falling")) u_R14 (
    .D(WD3__Data_to_write_in_the_register_of_address_A3), .en(E14), .Q(R14),
    .clk(Clk__Detects_changes_in_the_clock), .clr(Rst__Reset_every_register_to_0));
  Register #(.width(32), .trigger("falling")) u_R16 (
    .D(WD3__Data_to_write_in_the_register_of_address_A3), .en(E16), .Q(R16),
    .clk(Clk__Detects_changes_in_the_clock), .clr(Rst__Reset_every_register_to_0));
  Register #(.width(32), .trigger("falling")) u_R18 (
    .D(WD3__Data_to_write_in_the_register_of_address_A3), .en(E18), .Q(R18),
    .clk(Clk__Detects_changes_in_the_clock), .clr(Rst__Reset_every_register_to_0));
  Register #(.width(32), .trigger("falling")) u_R20 (
    .D(WD3__Data_to_write_in_the_register_of_address_A3), .en(E20), .Q(R20),
    .clk(Clk__Detects_changes_in_the_clock), .clr(Rst__Reset_every_register_to_0));
  Register #(.width(32), .trigger("falling")) u_R22 (
    .D(WD3__Data_to_write_in_the_register_of_address_A3), .en(E22), .Q(R22),
    .clk(Clk__Detects_changes_in_the_clock), .clr(Rst__Reset_every_register_to_0));
  Register #(.width(32), .trigger("falling")) u_R1 (
    .D(WD3__Data_to_write_in_the_register_of_address_A3), .en(E1), .Q(R1),
    .clk(Clk__Detects_changes_in_the_clock), .clr(Rst__Reset_every_register_to_0));
  Register #(.width(32), .trigger("falling")) u_R3 (
    .D(WD3__Data_to_write_in_the_register_of_address_A3), .en(E3), .Q(R3),
    .clk(Clk__Detects_changes_in_the_clock), .clr(Rst__Reset_every_register_to_0));
  Register #(.width(32), .trigger("falling")) u_R5 (
    .D(WD3__Data_to_write_in_the_register_of_address_A3), .en(E5), .Q(R5),
    .clk(Clk__Detects_changes_in_the_clock), .clr(Rst__Reset_every_register_to_0));
  Register #(.width(32), .trigger("falling")) u_R7 (
    .D(WD3__Data_to_write_in_the_register_of_address_A3), .en(E7), .Q(R7),
    .clk(Clk__Detects_changes_in_the_clock), .clr(Rst__Reset_every_register_to_0));
  Register #(.width(32), .trigger("falling")) u_R9 (
    .D(WD3__Data_to_write_in_the_register_of_address_A3), .en(E9), .Q(R9),
    .clk(Clk__Detects_changes_in_the_clock), .clr(Rst__Reset_every_register_to_0));
  Register #(.width(32), .trigger("falling")) u_R11 (
    .D(WD3__Data_to_write_in_the_register_of_address_A3), .en(E11), .Q(R11),
    .clk(Clk__Detects_changes_in_the_clock), .clr(Rst__Reset_every_register_to_0));
  Register #(.width(32), .trigger("falling")) u_R13 (
    .D(WD3__Data_to_write_in_the_register_of_address_A3), .en(E13), .Q(R13),
    .clk(Clk__Detects_changes_in_the_clock), .clr(Rst__Reset_every_register_to_0));
  Register #(.width(32), .trigger("falling")) u_R15 (
    .D(WD3__Data_to_write_in_the_register_of_address_A3), .en(E15), .Q(R15),
    .clk(Clk__Detects_changes_in_the_clock), .clr(Rst__Reset_every_register_to_0));
  Register #(.width(32), .trigger("falling")) u_R17 (
    .D(WD3__Data_to_write_in_the_register_of_address_A3), .en(E17), .Q(R17),
    .clk(Clk__Detects_changes_in_the_clock), .clr(Rst__Reset_every_register_to_0));
  Register #(.width(32), .trigger("falling")) u_R19 (
    .D(WD3__Data_to_write_in_the_register_of_address_A3), .en(E19), .Q(R19),
    .clk(Clk__Detects_changes_in_the_clock), .clr(Rst__Reset_every_register_to_0));
  Register #(.width(32), .trigger("falling")) u_R21 (
    .D(WD3__Data_to_write_in_the_register_of_address_A3), .en(E21), .Q(R21),
    .clk(Clk__Detects_changes_in_the_clock), .clr(Rst__Reset_every_register_to_0));
  Register #(.width(32), .trigger("falling")) u_R23 (
    .D(WD3__Data_to_write_in_the_register_of_address_A3), .en(E23), .Q(R23),
    .clk(Clk__Detects_changes_in_the_clock), .clr(Rst__Reset_every_register_to_0));
  Register #(.width(32), .trigger("falling")) u_R24 (
    .D(WD3__Data_to_write_in_the_register_of_address_A3), .en(E24), .Q(R24),
    .clk(Clk__Detects_changes_in_the_clock), .clr(Rst__Reset_every_register_to_0));
  Register #(.width(32), .trigger("falling")) u_R26 (
    .D(WD3__Data_to_write_in_the_register_of_address_A3), .en(E26), .Q(R26),
    .clk(Clk__Detects_changes_in_the_clock), .clr(Rst__Reset_every_register_to_0));
  Register #(.width(32), .trigger("falling")) u_R28 (
    .D(WD3__Data_to_write_in_the_register_of_address_A3), .en(E28), .Q(R28),
    .clk(Clk__Detects_changes_in_the_clock), .clr(Rst__Reset_every_register_to_0));
  not not_1 (not_1_out, SSPW__When_1__A3_is_ignored_and_points_to_R31__R31_is_only_modified_if_SSP_is_enable);
  Multiplexer #(.select(5), .width(32), .enable("false")) multiplexer_1 (
    .in0(R0), .in1(R1), .in2(R2), .in3(R3), .in4(R4), .in5(R5), .in6(R6), .in7(R7), .in8(R8), .in9(R9),
    .in10(R10), .in11(R11), .in12(R12), .in13(R13), .in14(R14), .in15(R15), .in16(R16), .in17(R17),
    .in18(R18), .in19(R19), .in20(R20), .in21(R21), .in22(R22), .in23(R23), .in24(R24), .in25(R25),
    .in26(R26), .in27(R27), .in28(R28), .in29(R29), .in30(R30), .in31(SP),
    .out(RD1___Output__First_data_read), .sel(A1__Address_of_the_first_register_to_read));
  Decoder #(.select(5), .disabled(0)) decoder_1 (
    .out0(E0), .out1(E1), .out2(E2), .out3(E3), .out4(E4), .out5(E5), .out6(E6), .out7(E7), .out8(E8),
    .out9(E9), .out10(E10), .out11(E11), .out12(E12), .out13(E13), .out14(E14), .out15(E15), .out16(E16),
    .out17(E17), .out18(E18), .out19(E19), .out20(E20), .out21(E21), .out22(E22), .out23(E23), .out24(E24),
    .out25(E25), .out26(E26), .out27(E27), .out28(E28), .out29(E29), .out30(E30), .out31(E31),
    .sel(A3__Addres_of_the_third_register_to_write), .en(and_1_out));
  and and_1 (and_1_out, not_1_out, WE3__Enable_Disable_writing);
  Register #(.width(32), .trigger("falling")) u_R25 (
    .D(WD3__Data_to_write_in_the_register_of_address_A3), .en(E25), .Q(R25),
    .clk(Clk__Detects_changes_in_the_clock), .clr(Rst__Reset_every_register_to_0));
  Register #(.width(32), .trigger("falling")) u_R27 (
    .D(WD3__Data_to_write_in_the_register_of_address_A3), .en(E27), .Q(R27),
    .clk(Clk__Detects_changes_in_the_clock), .clr(Rst__Reset_every_register_to_0));
  Register #(.width(32), .trigger("falling")) u_R29 (
    .D(WD3__Data_to_write_in_the_register_of_address_A3), .en(E29), .Q(R29),
    .clk(Clk__Detects_changes_in_the_clock), .clr(Rst__Reset_every_register_to_0));
  Register #(.width(32), .trigger("falling")) u_R30 (
    .D(WD3__Data_to_write_in_the_register_of_address_A3), .en(E30), .Q(R30),
    .clk(Clk__Detects_changes_in_the_clock), .clr(Rst__Reset_every_register_to_0));
  Register #(.width(32), .trigger("falling")) R31_SP (
    .D(WD3__Data_to_write_in_the_register_of_address_A3), .en(and_2_out), .Q(SP),
    .clk(Clk__Detects_changes_in_the_clock), .clr(Rst__Reset_every_register_to_0));
  and and_2 (and_2_out, WE3__Enable_Disable_writing, SSPW__When_1__A3_is_ignored_and_points_to_R31__R31_is_only_modified_if_SSP_is_enable);
  Multiplexer #(.select(5), .width(32), .enable("false")) multiplexer_2 (
    .in0(R0), .in1(R1), .in2(R2), .in3(R3), .in4(R4), .in5(R5), .in6(R6), .in7(R7), .in8(R8), .in9(R9),
    .in10(R10), .in11(R11), .in12(R12), .in13(R13), .in14(R14), .in15(R15), .in16(R16), .in17(R17),
    .in18(R18), .in19(R19), .in20(R20), .in21(R21), .in22(R22), .in23(R23), .in24(R24), .in25(R25),
    .in26(R26), .in27(R27), .in28(R28), .in29(R29), .in30(R30), .in31(SP),
    .out(RD2___Output__Second_data_read), .sel(A2__Address_of_the_second_register_to_read));

  // Other names for the same wires on the sheet: A1[4:0] = A1__Address_of_the_first_register_to_read;
  //   A2[4:0] = A2__Address_of_the_second_register_to_read; A3[4:0] = A3__Addres_of_the_third_register_to_write;
  //   Clk = Clk__Detects_changes_in_the_clock; RD1[31:0] = RD1___Output__First_data_read;
  //   RD2[31:0] = RD2___Output__Second_data_read; Rst = Rst__Reset_every_register_to_0;
  //   SSP = SSPW__When_1__A3_is_ignored_and_points_to_R31__R31_is_only_modified_if_SSP_is_enable;
  //   WD3[31:0] = WD3__Data_to_write_in_the_register_of_address_A3; WE3 = WE3__Enable_Disable_writing

  // Notes on the sheet:
  //   Input
  //   Registers
  //   Output
  //   Reading
  //   Writing
endmodule
