// Logisim project InstructionDecoder.circ as structural Verilog: 1 circuit, main circuit main
module main (
  input  [31:0] Instruction_Code,
  output [5:0] Func_Code,
  output [4:0] Rd,
  output [4:0] Rt,
  output [4:0] Rs,
  output [5:0] Op_Code,
  output [15:0] Inmediate,
  output [25:0] Jmp_Idx
);

  // Probe on Instruction_Code[10:6]

  assign Func_Code = Instruction_Code[5:0];
  assign Inmediate = Instruction_Code[15:0];
  assign Jmp_Idx = Instruction_Code[25:0];
  assign Op_Code = Instruction_Code[31:26];
  assign Rd = Instruction_Code[15:11];
  assign Rs = Instruction_Code[25:21];
  assign Rt = Instruction_Code[20:16];

  // Other names for the same wires on the sheet: Unused[4:0] = Instruction_Code[10:6]
endmodule
