// Logisim project MemInterfaz.circ as structural Verilog: 2 circuits, main circuit main
module main (
  input  Reset,
  input  [31:0] Address,
  input  Clock,
  input  [31:0] RAM_Out_0,
  input  REQ,
  input  RW,
  input  [31:0] RAM_Out_1,
  input  [31:0] Cache_In_0,
  input  [31:0] RAM_Out_2,
  input  [31:0] Cache_In_1,
  input  [31:0] RAM_Out_3,
  input  [31:0] Cache_In_2,
  input  [31:0] Cache_In_3,
  input  [3:0] Read_Time,
  input  [3:0] Write_Time,
  input  [3:0] RAM_MASK,
  output [3:0] Mask,
  output [15:0] Address_2,
  output [31:0] MEM_Out_0,
  output Ram_CS,
  output [31:0] MEM_Out_1,
  output [31:0] Data_Out_0,
  output [31:0] MEM_Out_2,
  output [31:0] Data_Out_1,
  output [31:0] MEM_Out_3,
  output [31:0] Data_Out_2,
  output Stall,
  output [31:0] Data_Out_3,
  output RW_2
);

  wire and_1_out, not_1_out, or_1_out, register_2_q;
  wire [3:0] multiplexer_2_out, register_1_q, subtractor_1_out, Target_Time;

  Multiplexer #(.width(4), .disabled(0), .enable("false")) multiplexer_1 (
    .in0(Read_Time), .in1(Write_Time), .out(Target_Time), .sel(RW));
  Multiplexer #(.width(4), .disabled(0), .enable("false")) multiplexer_2 (
    .in0(subtractor_1_out), .in1(Target_Time), .out(multiplexer_2_out), .sel(and_1_out));
  and and_1 (and_1_out, REQ, not_1_out);
  not not_1 (not_1_out, Stall);
  Register #(.width(4)) register_1 (.D(multiplexer_2_out), .en(or_1_out), .Q(register_1_q), .clk(Clock), .clr(Reset));
  or or_1 (or_1_out, Stall, REQ);
  Subtractor #(.width(4)) subtractor_1 (.a(register_1_q), .b(4'b0001), .out(subtractor_1_out));  // open: bin, bout
  Comparator #(.width(4)) comparator_1 (.a(register_1_q), .b(4'b0000), .gt(Stall));  // open: eq, lt
  Register #(.width(1)) register_2 (.D(Stall), .Q(register_2_q), .clk(Clock), .clr(Reset));  // open: en
  or or_2 (Ram_CS, Stall, register_2_q);
  Endian_Swapper endian_swapper_1 (.Data_In(RAM_Out_0), .out_2(MEM_Out_0));
  Endian_Swapper endian_swapper_2 (.Data_In(RAM_Out_1), .out_2(MEM_Out_1));
  Endian_Swapper endian_swapper_3 (.Data_In(RAM_Out_2), .out_2(MEM_Out_2));
  Endian_Swapper endian_swapper_4 (.Data_In(RAM_Out_3), .out_2(MEM_Out_3));
  Endian_Swapper endian_swapper_5 (.Data_In(Cache_In_0), .out_2(Data_Out_0));
  Endian_Swapper endian_swapper_6 (.Data_In(Cache_In_1), .out_2(Data_Out_1));
  Endian_Swapper endian_swapper_7 (.Data_In(Cache_In_2), .out_2(Data_Out_2));
  Endian_Swapper endian_swapper_8 (.Data_In(Cache_In_3), .out_2(Data_Out_3));

  assign Address_2 = Address[19:4];
  assign Mask = RAM_MASK;
  assign RW_2 = RW;

  // Other names for the same wires on the sheet: Addr[31:0] = Address; RAM_A[15:0] = Address[19:4]; CLK = Clock;
  //   Rst = Reset; RT[3:0] = Read_Time; WT[3:0] = Write_Time

  // Notes on the sheet:
  //   RAM ADDRESS
  //   DATA FROM CACHE
  //   MEM Out
  //   SEQUENCING
  //   DATA FROM RAM
  //   RAM TIMING
  //   DATA WRITE MASK
  //   RAM ADDRESS
  //   DATA TO RAM
endmodule

module Endian_Swapper (
  input  [31:0] Data_In,
  output [31:0] out_2
);


  assign out_2 = {Data_In[7:0], Data_In[15:8], Data_In[23:16], Data_In[31:24]};
endmodule
