// Logisim project s-mips.circ as structural Verilog: 6 circuits, main circuit S-MIPS Board
module S_MIPS_Board (
  input  DESHABILITAR_DISPATCHER,
  output halt
);

  wire button_1_out, CLK, CS, d_ff_1_q, LCLR, LoadRAM, LoadRAMOn, LW, R_R_W, R_W, ram_dispatcher_1_finished,
       RCS, Reset_out, RST, TTY_EN;
  wire [2:0] KDB;
  wire [3:0] LMask, Mask, ram_1_read_time, ram_1_write_time, RMask;
  wire [6:0] KDB_DATA, TTY_DATA;
  wire [15:0] Addr, LAddr, RAddr;
  wire [31:0] I0, I1, I2, I3, LData, ram_1_data_out_0, ram_1_data_out_1, ram_1_data_out_2, ram_1_data_out_3,
       RI0, RI1, RI2, RI3;

  TTY #(.rows(25), .cols(80)) tty_1 (.data(TTY_DATA), .clk(CLK), .we(TTY_EN), .clr(RST));
  not not_1 (LoadRAMOn, ram_dispatcher_1_finished);
  RAM_Dispatcher ram_dispatcher_1 (
    .WriteTime(ram_1_write_time), .Clock(CLK), .Data(LData), .Address(LAddr), .Mask(LMask),
    .Finished(ram_dispatcher_1_finished), .Write(LW), .CLR(LCLR));
  Keyboard #(.buflen(64)) keyboard_1 (.clk(CLK), .re(KDB[0]), .avail(KDB[2]), .data(KDB_DATA));  // open: clr
  RAM ram_1 (
    .Address(RAddr), .Data_Out_0(ram_1_data_out_0), .Data_Out_1(ram_1_data_out_1),
    .Data_Out_2(ram_1_data_out_2), .Data_Out_3(ram_1_data_out_3), .Data_In_0(RI0), .Data_In_1(RI1),
    .Data_In_2(RI2), .Data_In_3(RI3), .Mask(RMask), .nRead_Write(R_R_W), .Chip_Select(RCS),
    .Read_Time(ram_1_read_time), .Reset(button_1_out), .Write_Time(ram_1_write_time));
  Button button_1 (.out(button_1_out));
  D_Flip_Flop d_ff_1 (.clk(CLK), .D(1'b1), .Q(d_ff_1_q), .reset(Reset_out));  // open: Qn, preset, en
  Button Reset (.out(Reset_out));
  S_MIPS s_mips_1 (
    .Kbd_Enable(KDB[0]), .Address(Addr), .Kbd_Clear(KDB[1]), .Kbd_Available(KDB[2]), .RAM_In_0(I0),
    .Kbd_ASCII_Data(KDB_DATA), .RAM_In_1(I1), .TTY_Enable(TTY_EN), .RAM_In_2(I2), .RAM_In_3(I3),
    .TTY_ASCII_Data(TTY_DATA), .Reset(RST), .RAM_Out_0(ram_1_data_out_0), .Clock(CLK),
    .RAM_Out_1(ram_1_data_out_1), .Stop(halt), .RAM_Out_2(ram_1_data_out_2), .RAM_Out_3(ram_1_data_out_3),
    .Mask(Mask), .Read_Time(ram_1_read_time), .Write_Time(ram_1_write_time), .nRead_Write(R_W),
    .Chip_Select(CS));
  D_Flip_Flop d_ff_2 (.clk(CLK), .D(d_ff_1_q), .Qn(LCLR), .reset(Reset_out));  // open: Q, preset, en
  or or_1 (RST, LCLR, LoadRAM);
  Clock clock_1 (.out(CLK));
  Multiplexer #(.width(32), .enable("false")) multiplexer_1 (.in0(I0), .in1(LData), .out(RI0), .sel(LoadRAM));
  Multiplexer #(.width(32), .enable("false")) multiplexer_2 (.in0(I1), .in1(LData), .out(RI1), .sel(LoadRAM));
  Multiplexer #(.width(32), .enable("false")) multiplexer_3 (.in0(I2), .in1(LData), .out(RI2), .sel(LoadRAM));
  Multiplexer #(.width(32), .enable("false")) multiplexer_4 (.in0(I3), .in1(LData), .out(RI3), .sel(LoadRAM));
  and and_1 (LoadRAM, ~DESHABILITAR_DISPATCHER, LoadRAMOn);  // AND_Gate
  Multiplexer #(.width(16), .enable("false")) multiplexer_5 (.in0(Addr), .in1(LAddr), .out(RAddr), .sel(LoadRAM));
  Multiplexer #(.width(4), .enable("false")) multiplexer_6 (.in0(Mask), .in1(LMask), .out(RMask), .sel(LoadRAM));
  Multiplexer #(.enable("false")) multiplexer_7 (.in0(CS), .in1(LW), .out(RCS), .sel(LoadRAM));
  Multiplexer #(.enable("false")) multiplexer_8 (.in0(R_W), .in1(LW), .out(R_R_W), .sel(LoadRAM));

  // Notes on the sheet:
  //   NO MODIFICAR
  //   Keyboard
endmodule

module RAM (
  input  [15:0] Address,
  input  [31:0] Data_In_0,
  input  [31:0] Data_In_1,
  input  [31:0] Data_In_2,
  input  [31:0] Data_In_3,
  input  [3:0] Mask,
  input  nRead_Write,
  input  Chip_Select,
  input  Reset,
  output [31:0] Data_Out_0,
  output [31:0] Data_Out_1,
  output [31:0] Data_Out_2,
  output [31:0] Data_Out_3,
  output [3:0] Read_Time,
  output [3:0] Write_Time
);

  wire and_2_out, and_3_out, and_4_out, and_5_out, and_6_out, and_7_out, and_8_out, and_9_out, Changed, CLK,
       comparator_2_eq, comparator_3_eq, comparator_4_eq, comparator_5_eq, comparator_6_eq, Count,
       demultiplexer_3_out0, Idle, Idle_q, Load, Load0, Load1, nand_1_out, or_1_out, or_2_out, or_3_out,
       or_4_out, or_5_out, or_6_out, or_7_out, or_8_out, or_9_out, or_10_out, Proc_q, Update_Mem, Zero_Time;
  wire [3:0] counter_1_q, multiplexer_1_out, subtractor_1_out;
  wire [31:0] register_1_q, register_2_q, register_3_q, register_4_q, register_5_q;

  // Probe on 4'b0011
  // Probe on 4'b0010
  Multiplexer #(.width(4), .enable("false")) multiplexer_1 (
    .in0(4'b0011), .in1(4'b0010), .out(multiplexer_1_out), .sel(nRead_Write));
  or or_1 (or_1_out, Idle, Update_Mem);
  or or_2 (or_2_out, ~Chip_Select, Reset);  // OR_Gate
  Subtractor #(.width(4)) subtractor_1 (.a(multiplexer_1_out), .b(4'b0010), .out(subtractor_1_out));  // open: bin, bout
  Demultiplexer #(.enable("false")) demultiplexer_1 (.out0(Idle), .out1(Load0), .in(Idle_q), .sel(Changed));
  D_Flip_Flop u_Idle (.clk(CLK), .D(or_1_out), .Q(Idle_q), .preset(or_2_out));  // open: Qn, en, reset
  // Probe on counter_1_q
  Counter #(.width(4), .max('hf)) counter_1 (
    .load(Load), .D(subtractor_1_out), .count(Count), .Q(counter_1_q), .clk(CLK), .clr(or_3_out));  // open: carry
  or or_3 (or_3_out, ~Chip_Select, Reset);  // OR_Gate
  Comparator #(.width(4), .mode("unsigned")) comparator_1 (
    .a(4'b0000), .b(counter_1_q), .eq(Zero_Time));  // open: gt, lt
  or or_4 (or_4_out, Count, Load0, Load1);
  Register #(.width(32)) register_1 (.D(Data_In_0), .en(Chip_Select), .Q(register_1_q), .clk(CLK), .clr(or_5_out));
  or or_5 (or_5_out, ~Chip_Select, Reset);  // OR_Gate
  Register #(.width(32)) register_2 (.D(Data_In_1), .en(Chip_Select), .Q(register_2_q), .clk(CLK), .clr(or_6_out));
  or or_6 (or_6_out, ~Chip_Select, Reset);  // OR_Gate
  Register #(.width(32)) register_3 (.D(Data_In_2), .en(Chip_Select), .Q(register_3_q), .clk(CLK), .clr(or_7_out));
  or or_7 (or_7_out, ~Chip_Select, Reset);  // OR_Gate
  Register #(.width(32)) register_4 (.D(Data_In_3), .en(Chip_Select), .Q(register_4_q), .clk(CLK), .clr(or_8_out));
  or or_8 (or_8_out, ~Chip_Select, Reset);  // OR_Gate
  Register #(.width(32)) register_5 (
    .D({{11{1'b1}}, nRead_Write, Mask, Address}), .en(Chip_Select), .Q(register_5_q), .clk(CLK),
    .clr(or_9_out));
  or or_9 (or_9_out, ~Chip_Select, Reset);  // OR_Gate
  D_Flip_Flop Proc (.clk(CLK), .D(or_4_out), .Q(Proc_q), .reset(or_10_out));  // open: Qn, preset, en
  or or_10 (or_10_out, ~Chip_Select, Reset);  // OR_Gate
  Demultiplexer #(.enable("false")) demultiplexer_2 (
    .out0(Count), .out1(Update_Mem), .in(demultiplexer_3_out0), .sel(Zero_Time));
  Demultiplexer #(.enable("false")) demultiplexer_3 (
    .out0(demultiplexer_3_out0), .out1(Load1), .in(Proc_q), .sel(Changed));
  Clock clock_1 (.out(CLK));
  Comparator #(.width(32)) comparator_2 (.a(register_1_q), .b(Data_In_0), .eq(comparator_2_eq));  // open: gt, lt
  Comparator #(.width(32)) comparator_3 (.a(register_2_q), .b(Data_In_1), .eq(comparator_3_eq));  // open: gt, lt
  Comparator #(.width(32)) comparator_4 (.a(register_3_q), .b(Data_In_2), .eq(comparator_4_eq));  // open: gt, lt
  Comparator #(.width(32)) comparator_5 (.a(register_4_q), .b(Data_In_3), .eq(comparator_5_eq));  // open: gt, lt
  Comparator #(.width(32)) comparator_6 (
    .a(register_5_q), .b({{11{1'b1}}, nRead_Write, Mask, Address}), .eq(comparator_6_eq));  // open: gt, lt
  nand nand_1 (nand_1_out, comparator_6_eq, comparator_2_eq, comparator_3_eq, comparator_4_eq, comparator_5_eq);
  and and_1 (Changed, nand_1_out, Chip_Select);
  or or_11 (Load, Count, Load1, Load0);
  and and_2 (and_2_out, Mask[0], Update_Mem, nRead_Write);
  and and_3 (and_3_out, Mask[1], Update_Mem, nRead_Write);
  and and_4 (and_4_out, Mask[2], Update_Mem, nRead_Write);
  and and_5 (and_5_out, Mask[3], Update_Mem, nRead_Write);
  RAM_part #(.addrWidth(16), .dataWidth(32), .bus("separate")) ram_1 (
    .addr(Address), .din(Data_In_0), .data(Data_Out_0), .str(and_2_out), .sel(Chip_Select), .clk(CLK),
    .ld(and_6_out), .clr(Reset));
  and and_6 (and_6_out, ~nRead_Write, Idle);  // AND_Gate
  RAM_part #(.addrWidth(16), .dataWidth(32), .bus("separate")) ram_2 (
    .addr(Address), .din(Data_In_1), .data(Data_Out_1), .str(and_3_out), .sel(Chip_Select), .clk(CLK),
    .ld(and_7_out), .clr(Reset));
  and and_7 (and_7_out, ~nRead_Write, Idle);  // AND_Gate
  RAM_part #(.addrWidth(16), .dataWidth(32), .bus("separate")) ram_3 (
    .addr(Address), .din(Data_In_2), .data(Data_Out_2), .str(and_4_out), .sel(Chip_Select), .clk(CLK),
    .ld(and_8_out), .clr(Reset));
  and and_8 (and_8_out, ~nRead_Write, Idle);  // AND_Gate
  RAM_part #(.addrWidth(16), .dataWidth(32), .bus("separate")) ram_4 (
    .addr(Address), .din(Data_In_3), .data(Data_Out_3), .str(and_5_out), .sel(Chip_Select), .clk(CLK),
    .ld(and_9_out), .clr(Reset));
  and and_9 (and_9_out, ~nRead_Write, Idle);  // AND_Gate

  assign Read_Time = 4'b0011;
  assign Write_Time = 4'b0010;

  // Other names for the same wires on the sheet: M0 = Mask[0]; M1 = Mask[1]; M2 = Mask[2]; M3 = Mask[3];
  //   RW = nRead_Write; CLR = Reset; CS = Chip_Select; Load2 = Count

  // Notes on the sheet:
  //   NO MODIFICAR
  //   excepto quizás los valores RT y WT
  //   BANK0
  //   BANK1
  //   BANK2
  //   BANK3
endmodule

module RAM_Dispatcher (
  input  [3:0] WriteTime,
  input  Clock,
  input  CLR,
  output [31:0] Data,
  output [15:0] Address,
  output [3:0] Mask,
  output Finished,
  output Write
);

  wire demultiplexer_2_out1, demultiplexer_3_out1, End, IDLE_q, IncAddr, Load, or_1_out, or_2_out, While_q,
       WriteEnd;
  wire [3:0] counter_1_q;
  wire [31:0] CurrentAddress_q;

  Counter #(.width(32), .max('hffffffff)) CurrentAddress (
    .count(IncAddr), .Q({CurrentAddress_q[31:18], Address, CurrentAddress_q[1:0]}), .clk(Clock), .clr(CLR));  // open: load, D, carry
  or or_1 (or_1_out, IncAddr, demultiplexer_3_out1, Finished);
  D_Flip_Flop IDLE (.clk(Clock), .D(or_1_out), .Q(IDLE_q), .preset(CLR));  // open: Qn, en, reset
  Demultiplexer #(.enable("false")) demultiplexer_1 (.out0(Load), .out1(Finished), .in(IDLE_q), .sel(End));
  D_Flip_Flop While (.clk(Clock), .D(or_2_out), .Q(While_q), .reset(CLR));  // open: Qn, preset, en
  or or_2 (or_2_out, Write, Load);
  RAM_part #(.addrWidth(18), .dataWidth(32)) ram_1 (
    .addr({Address, CurrentAddress_q[1:0]}), .data(Data), .clk(Clock));  // open: sel, ld, clr
  Demultiplexer #(.enable("false")) demultiplexer_2 (
    .out0(Write), .out1(demultiplexer_2_out1), .in(While_q), .sel(WriteEnd));
  Decoder #(.select(2)) decoder_1 (
    .out0(Mask[0]), .out1(Mask[1]), .out2(Mask[2]), .out3(Mask[3]), .sel(CurrentAddress_q[1:0]));  // open: en
  Demultiplexer #(.enable("false")) demultiplexer_3 (
    .out0(IncAddr), .out1(demultiplexer_3_out1), .in(demultiplexer_2_out1), .sel(End));
  Counter #(.width(4), .max('hf)) counter_1 (
    .load(Load), .D(WriteTime), .count(Write), .Q(counter_1_q), .clk(Clock));  // open: carry, clr
  Comparator #(.width(32)) comparator_1 (.a(Data), .b({32{1'b1}}), .eq(End));  // open: gt, lt
  Comparator #(.width(4)) comparator_2 (.a(4'b0000), .b(counter_1_q), .eq(WriteEnd));  // open: gt, lt

  // Other names for the same wires on the sheet: CLK = Clock; Count = Write; WT[3:0] = WriteTime
endmodule

module S_MIPS (
  input  Kbd_Available,
  input  [6:0] Kbd_ASCII_Data,
  input  [31:0] RAM_Out_0,
  input  [31:0] RAM_Out_1,
  input  Reset,
  input  [31:0] RAM_Out_2,
  input  Clock,
  input  [31:0] RAM_Out_3,
  input  [3:0] Read_Time,
  input  [3:0] Write_Time,
  output Kbd_Enable,
  output [15:0] Address,
  output Kbd_Clear,
  output TTY_Enable,
  output [6:0] TTY_ASCII_Data,
  output Stop,
  output [31:0] RAM_In_0,
  output [31:0] RAM_In_1,
  output [31:0] RAM_In_2,
  output [31:0] RAM_In_3,
  output [3:0] Mask,
  output nRead_Write,
  output Chip_Select
);


  // Other names for the same wires on the sheet: CLK = Clock; CLR = Reset; CS = Chip_Select;
  //   KBD_AVAIL = Kbd_Available; KBD_CLR = Kbd_Clear; KBD_DATA[6:0] = Kbd_ASCII_Data; RAM_A[15:0] = Address;
  //   RAM_INPUT_0[31:0] = RAM_In_0; RAM_INPUT_1[31:0] = RAM_In_1; RAM_INPUT_2[31:0] = RAM_In_2;
  //   RAM_INPUT_3[31:0] = RAM_In_3; RAM_MASK[3:0] = Mask; RAM_OUTPUT_0[31:0] = RAM_Out_0;
  //   RAM_OUTPUT_1[31:0] = RAM_Out_1; RAM_OUTPUT_2[31:0] = RAM_Out_2; RAM_OUTPUT_3[31:0] = RAM_Out_3;
  //   RW = nRead_Write; TTY_DATA[6:0] = TTY_ASCII_Data

  // Notes on the sheet:
  //   RAM ADDRESS
  //   DATA FROM RAM
  //   DATA TO RAM
  //   DATA WRITE MASK
  //   RAM TIMING
  //   RAM CONTROL
  //   KEYBOARD
  //   TTY
  //   SEQUENCING
endmodule

module DataPath (
  input  [31:0] PCD__Data_to_write_PC,
  input  [31:0] IRD__Data_to_write_IR__Instruction_Register,
  input  EPC,
  input  EIR,
  input  [31:0] MDRD__Data_to_write_MDR__Memory_Data_Register,
  input  [31:0] ALUD__Data_to_write_ALUOut__ALUOut_Register,
  input  EMDR,
  input  EALUOut,
  input  [31:0] HiD__Data_to_rewrite_Hi,
  input  [31:0] LoD__Data_to_rewrite_Lo,
  input  EHi,
  input  ELo,
  input  [31:0] Const,
  input  ER__Enable_Reading,
  input  [4:0] A3__Direction_of_register_to_write,
  input  [4:0] A1__Direction_of_first_register_to_read,
  input  [31:0] WD3__Data_to_write,
  input  [4:0] A2__Direction_of_second_register_to_read,
  input  IorDS__Selector_of_Dir_output__0_returns_PC__1_returns_ALUOut,
  input  WE3__Enable_writing,
  input  [1:0] SSrcA__Selector_of_SrcA_output__0_returns_PC__1_returns_A__2_returns_jPC_and_3_returns_PC_ISd4,
  input  [1:0] SSrcB__Selector_of_SrcB_output__0_returns_4__1_returns_B__2_returns_IS_and_3_returns_ISd4,
  input  SIS__Selector_of_type_of_constant__when_0_const_is_used_as_I15Const__when_1_it_s_0Const,
  input  ESrcB__When_0_SrcB_returns_0,
  input  Clk,
  input  Rst,
  output [31:0] PC,
  output [31:0] IR,
  output [31:0] MDR,
  output [31:0] ALUOut,
  output [31:0] Hi,
  output [31:0] Lo,
  output [31:0] A,
  output [31:0] B,
  output [31:0] IR_2,
  output [31:0] ALUSrcA,
  output [31:0] ALUSrcB
);

  wire [31:0] _0Const, AD, BD, I15Const, IS, ISd4, multiplexer_3_out, multiplexer_4_out, PC_ISd4;

  Multiplexer #(.width(32), .enable("false")) multiplexer_1 (
    .in0(PC), .in1(ALUOut), .out(IR_2), .sel(IorDS__Selector_of_Dir_output__0_returns_PC__1_returns_ALUOut));
  Multiplexer #(.width(32), .enable("false")) multiplexer_2 (
    .in0(I15Const), .in1(_0Const), .out(IS),
    .sel(SIS__Selector_of_type_of_constant__when_0_const_is_used_as_I15Const__when_1_it_s_0Const));
  assign I15Const = {{16{Const[15]}}, Const[15:0]};  // Bit_Extender bit_extender_1
  assign _0Const = {{16{1'b0}}, Const[15:0]};  // Bit_Extender bit_extender_2
  Shifter #(.width(32)) shifter_1 (.in(IS), .\dist (5'b00010), .out(ISd4));
  Register #(.width(32)) u_PC (.D(PCD__Data_to_write_PC), .en(EPC), .Q(PC), .clk(Clk), .clr(Rst));
  Register #(.width(32)) u_MDR (
    .D(MDRD__Data_to_write_MDR__Memory_Data_Register), .en(EMDR), .Q(MDR), .clk(Clk), .clr(Rst));
  Register #(.width(32)) u_Hi (.D(HiD__Data_to_rewrite_Hi), .en(EHi), .Q(Hi), .clk(Clk), .clr(Rst));
  Register #(.width(32)) u_A (.D(AD), .en(ER__Enable_Reading), .Q(A), .clk(Clk), .clr(Rst));
  Register_File register_file_1 (
    .Clk__Detects_changes_in_the_clock(Clk),
    .A1__Address_of_the_first_register_to_read(A1__Direction_of_first_register_to_read),
    .A2__Address_of_the_second_register_to_read(A2__Direction_of_second_register_to_read),
    .A3__Addres_of_the_third_register_to_write(A3__Direction_of_register_to_write),
    .WD3__Data_to_write_in_the_register_of_address_A3(WD3__Data_to_write),
    .WE3__Enable_Disable_writing(WE3__Enable_writing), .Rst__Reset_every_register_to_0(Rst),
    .RD1___Output__First_data_read(AD), .RD2___Output__Second_data_read(BD));
  Multiplexer #(.width(32), .enable("false")) multiplexer_3 (
    .in0(B), .in1(BD), .out(multiplexer_3_out), .sel(ER__Enable_Reading));
  Adder #(.width(32)) adder_1 (.a(PC), .b(ISd4), .out(PC_ISd4));  // open: cin, cout
  Register #(.width(32)) u_IR (.D(IRD__Data_to_write_IR__Instruction_Register), .en(EIR), .Q(IR), .clk(Clk), .clr(Rst));
  Register #(.width(32)) u_ALUOut (
    .D(ALUD__Data_to_write_ALUOut__ALUOut_Register), .en(EALUOut), .Q(ALUOut), .clk(Clk), .clr(Rst));
  Register #(.width(32)) u_Lo (.D(LoD__Data_to_rewrite_Lo), .en(ELo), .Q(Lo), .clk(Clk), .clr(Rst));
  Register #(.width(32)) u_B (.D(BD), .en(ER__Enable_Reading), .Q(B), .clk(Clk), .clr(Rst));
  Multiplexer #(.width(32), .enable("false")) multiplexer_4 (
    .in0(A), .in1(AD), .out(multiplexer_4_out), .sel(ER__Enable_Reading));
  Multiplexer #(.select(2), .width(32), .enable("false")) multiplexer_5 (
    .in0(PC), .in1(multiplexer_4_out), .in2({PC[31:28], Const[25:0], 2'b00}), .in3(PC_ISd4), .out(ALUSrcA),
    .sel(SSrcA__Selector_of_SrcA_output__0_returns_PC__1_returns_A__2_returns_jPC_and_3_returns_PC_ISd4));
  Multiplexer #(.select(2), .width(32), .disabled(0)) multiplexer_6 (
    .in0(32'h4), .in1(multiplexer_3_out), .in2(IS), .in3(ISd4), .out(ALUSrcB),
    .sel(SSrcB__Selector_of_SrcB_output__0_returns_4__1_returns_B__2_returns_IS_and_3_returns_ISd4),
    .en(ESrcB__When_0_SrcB_returns_0));

  // Other names for the same wires on the sheet: A1[4:0] = A1__Direction_of_first_register_to_read;
  //   A2[4:0] = A2__Direction_of_second_register_to_read; A3[4:0] = A3__Direction_of_register_to_write;
  //   ALUD[31:0] = ALUD__Data_to_write_ALUOut__ALUOut_Register; Dir[31:0] = IR_2; ER = ER__Enable_Reading;
  //   ESrcB = ESrcB__When_0_SrcB_returns_0; HiD[31:0] = HiD__Data_to_rewrite_Hi;
  //   IorDS = IorDS__Selector_of_Dir_output__0_returns_PC__1_returns_ALUOut;
  //   IRD[31:0] = IRD__Data_to_write_IR__Instruction_Register; jPC[31:2] = {PC[31:28], Const[25:0]};
  //   LoD[31:0] = LoD__Data_to_rewrite_Lo; MDRD[31:0] = MDRD__Data_to_write_MDR__Memory_Data_Register;
  //   PCD[31:0] = PCD__Data_to_write_PC;
  //   SIS = SIS__Selector_of_type_of_constant__when_0_const_is_used_as_I15Const__when_1_it_s_0Const;
  //   SSrcA[1:0] = SSrcA__Selector_of_SrcA_output__0_returns_PC__1_returns_A__2_returns_jPC_and_3_returns_PC_ISd4;
  //   SSrcB[1:0] = SSrcB__Selector_of_SrcB_output__0_returns_4__1_returns_B__2_returns_IS_and_3_returns_ISd4;
  //   WD3[31:0] = WD3__Data_to_write; WE3 = WE3__Enable_writing

  // Notes on the sheet:
  //   Input
  //   Output
  //   Registers
  //   Multiplexers and Operations
endmodule

module Register_File (
  input  Clk__Detects_changes_in_the_clock,
  input  [4:0] A1__Address_of_the_first_register_to_read,
  input  [4:0] A2__Address_of_the_second_register_to_read,
  input  [4:0] A3__Addres_of_the_third_register_to_write,
  input  [31:0] WD3__Data_to_write_in_the_register_of_address_A3,
  input  WE3__Enable_Disable_writing,
  input  Rst__Reset_every_register_to_0,
  output [31:0] RD1___Output__First_data_read,
  output [31:0] RD2___Output__Second_data_read
);

  wire E0, E1, E2, E3, E4, E5, E6, E7, E8, E9, E10, E11, E12, E13, E14, E15, E16, E17, E18, E19, E20, E21,
       E22, E23, E24, E25, E26, E27, E28, E29, E30, E31;
  wire [31:0] R0, R1, R2, R3, R4, R5, R6, R7, R8, R9, R10, R11, R12, R13, R14, R15, R16, R17, R18, R19, R20,
       R21, R22, R23, R24, R25, R26, R27, R28, R29, R30, SP;

  Register #(.width(32)) u_R0 (
    .D({32{1'b0}}), .en(E0), .Q(R0), .clk(Clk__Detects_changes_in_the_clock),
    .clr(Rst__Reset_every_register_to_0));
  Register #(.width(32)) u_R2 (
    .D(WD3__Data_to_write_in_the_register_of_address_A3), .en(E2), .Q(R2),
    .clk(Clk__Detects_changes_in_the_clock), .clr(Rst__Reset_every_register_to_0));
  Register #(.width(32)) u_R4 (
    .D(WD3__Data_to_write_in_the_register_of_address_A3), .en(E4), .Q(R4),
    .clk(Clk__Detects_changes_in_the_clock), .clr(Rst__Reset_every_register_to_0));
  Register #(.width(32)) u_R6 (
    .D(WD3__Data_to_write_in_the_register_of_address_A3), .en(E6), .Q(R6),
    .clk(Clk__Detects_changes_in_the_clock), .clr(Rst__Reset_every_register_to_0));
  Register #(.width(32)) u_R8 (
    .D(WD3__Data_to_write_in_the_register_of_address_A3), .en(E8), .Q(R8),
    .clk(Clk__Detects_changes_in_the_clock), .clr(Rst__Reset_every_register_to_0));
  Register #(.width(32)) u_R10 (
    .D(WD3__Data_to_write_in_the_register_of_address_A3), .en(E10), .Q(R10),
    .clk(Clk__Detects_changes_in_the_clock), .clr(Rst__Reset_every_register_to_0));
  Register #(.width(32)) u_R12 (
    .D(WD3__Data_to_write_in_the_register_of_address_A3), .en(E12), .Q(R12),
    .clk(Clk__Detects_changes_in_the_clock), .clr(Rst__Reset_every_register_to_0));
  Register #(.width(32)) u_R14 (
    .D(WD3__Data_to_write_in_the_register_of_address_A3), .en(E14), .Q(R14),
    .clk(Clk__Detects_changes_in_the_clock), .clr(Rst__Reset_every_register_to_0));
  Register #(.width(32)) u_R16 (
    .D(WD3__Data_to_write_in_the_register_of_address_A3), .en(E16), .Q(R16),
    .clk(Clk__Detects_changes_in_the_clock), .clr(Rst__Reset_every_register_to_0));
  Register #(.width(32)) u_R18 (
    .D(WD3__Data_to_write_in_the_register_of_address_A3), .en(E18), .Q(R18),
    .clk(Clk__Detects_changes_in_the_clock), .clr(Rst__Reset_every_register_to_0));
  Register #(.width(32)) u_R20 (
    .D(WD3__Data_to_write_in_the_register_of_address_A3), .en(E20), .Q(R20),
    .clk(Clk__Detects_changes_in_the_clock), .clr(Rst__Reset_every_register_to_0));
  Register #(.width(32)) u_R22 (
    .D(WD3__Data_to_write_in_the_register_of_address_A3), .en(E22), .Q(R22),
    .clk(Clk__Detects_changes_in_the_clock), .clr(Rst__Reset_every_register_to_0));
  Register #(.width(32)) u_R1 (
    .D(WD3__Data_to_write_in_the_register_of_address_A3), .en(E1), .Q(R1),
    .clk(Clk__Detects_changes_in_the_clock), .clr(Rst__Reset_every_register_to_0));
  Register #(.width(32)) u_R3 (
    .D(WD3__Data_to_write_in_the_register_of_address_A3), .en(E3), .Q(R3),
    .clk(Clk__Detects_changes_in_the_clock), .clr(Rst__Reset_every_register_to_0));
  Register #(.width(32)) u_R5 (
    .D(WD3__Data_to_write_in_the_register_of_address_A3), .en(E5), .Q(R5),
    .clk(Clk__Detects_changes_in_the_clock), .clr(Rst__Reset_every_register_to_0));
  Register #(.width(32)) u_R7 (
    .D(WD3__Data_to_write_in_the_register_of_address_A3), .en(E7), .Q(R7),
    .clk(Clk__Detects_changes_in_the_clock), .clr(Rst__Reset_every_register_to_0));
  Register #(.width(32)) u_R9 (
    .D(WD3__Data_to_write_in_the_register_of_address_A3), .en(E9), .Q(R9),
    .clk(Clk__Detects_changes_in_the_clock), .clr(Rst__Reset_every_register_to_0));
  Register #(.width(32)) u_R11 (
    .D(WD3__Data_to_write_in_the_register_of_address_A3), .en(E11), .Q(R11),
    .clk(Clk__Detects_changes_in_the_clock), .clr(Rst__Reset_every_register_to_0));
  Register #(.width(32)) u_R13 (
    .D(WD3__Data_to_write_in_the_register_of_address_A3), .en(E13), .Q(R13),
    .clk(Clk__Detects_changes_in_the_clock), .clr(Rst__Reset_every_register_to_0));
  Register #(.width(32)) u_R15 (
    .D(WD3__Data_to_write_in_the_register_of_address_A3), .en(E15), .Q(R15),
    .clk(Clk__Detects_changes_in_the_clock), .clr(Rst__Reset_every_register_to_0));
  Register #(.width(32)) u_R17 (
    .D(WD3__Data_to_write_in_the_register_of_address_A3), .en(E17), .Q(R17),
    .clk(Clk__Detects_changes_in_the_clock), .clr(Rst__Reset_every_register_to_0));
  Register #(.width(32)) u_R19 (
    .D(WD3__Data_to_write_in_the_register_of_address_A3), .en(E19), .Q(R19),
    .clk(Clk__Detects_changes_in_the_clock), .clr(Rst__Reset_every_register_to_0));
  Register #(.width(32)) u_R21 (
    .D(WD3__Data_to_write_in_the_register_of_address_A3), .en(E21), .Q(R21),
    .clk(Clk__Detects_changes_in_the_clock), .clr(Rst__Reset_every_register_to_0));
  Register #(.width(32)) u_R23 (
    .D(WD3__Data_to_write_in_the_register_of_address_A3), .en(E23), .Q(R23),
    .clk(Clk__Detects_changes_in_the_clock), .clr(Rst__Reset_every_register_to_0));
  Register #(.width(32)) u_R24 (
    .D(WD3__Data_to_write_in_the_register_of_address_A3), .en(E24), .Q(R24),
    .clk(Clk__Detects_changes_in_the_clock), .clr(Rst__Reset_every_register_to_0));
  Register #(.width(32)) u_R26 (
    .D(WD3__Data_to_write_in_the_register_of_address_A3), .en(E26), .Q(R26),
    .clk(Clk__Detects_changes_in_the_clock), .clr(Rst__Reset_every_register_to_0));
  Register #(.width(32)) u_R28 (
    .D(WD3__Data_to_write_in_the_register_of_address_A3), .en(E28), .Q(R28),
    .clk(Clk__Detects_changes_in_the_clock), .clr(Rst__Reset_every_register_to_0));
  Multiplexer #(.select(5), .width(32), .enable("false")) multiplexer_1 (
    .in0(R0), .in1(R1), .in2(R2), .in3(R3), .in4(R4), .in5(R5), .in6(R6), .in7(R7), .in8(R8), .in9(R9),
    .in10(R10), .in11(R11), .in12(R12), .in13(R13), .in14(R14), .in15(R15), .in16(R16), .in17(R17),
    .in18(R18), .in19(R19), .in20(R20), .in21(R21), .in22(R22), .in23(R23), .in24(R24), .in25(R25),
    .in26(R26), .in27(R27), .in28(R28), .in29(R29), .in30(R30), .in31(SP),
    .out(RD1___Output__First_data_read), .sel(A1__Address_of_the_first_register_to_read));
  Decoder #(.select(5), .disabled(0)) decoder_1 (
    .out0(E0), .out1(E1), .out2(E2), .out3(E3), .out4(E4), .out5(E5), .out6(E6), .out7(E7), .out8(E8),
    .out9(E9), .out10(E10), .out11(E11), .out12(E12), .out13(E13), .out14(E14), .out15(E15), .out16(E16),
    .out17(E17), .out18(E18), .out19(E19), .out20(E20), .out21(E21), .out22(E22), .out23(E23), .out24(E24),
    .out25(E25), .out26(E26), .out27(E27), .out28(E28), .out29(E29), .out30(E30), .out31(E31),
    .sel(A3__Addres_of_the_third_register_to_write), .en(WE3__Enable_Disable_writing));
  Register #(.width(32)) u_R25 (
    .D(WD3__Data_to_write_in_the_register_of_address_A3), .en(E25), .Q(R25),
    .clk(Clk__Detects_changes_in_the_clock), .clr(Rst__Reset_every_register_to_0));
  Register #(.width(32)) u_R27 (
    .D(WD3__Data_to_write_in_the_register_of_address_A3), .en(E27), .Q(R27),
    .clk(Clk__Detects_changes_in_the_clock), .clr(Rst__Reset_every_register_to_0));
  Register #(.width(32)) u_R29 (
    .D(WD3__Data_to_write_in_the_register_of_address_A3), .en(E29), .Q(R29),
    .clk(Clk__Detects_changes_in_the_clock), .clr(Rst__Reset_every_register_to_0));
  Register #(.width(32)) u_R30 (
    .D(WD3__Data_to_write_in_the_register_of_address_A3), .en(E30), .Q(R30),
    .clk(Clk__Detects_changes_in_the_clock), .clr(Rst__Reset_every_register_to_0));
  Register #(.width(32)) R31_SP (
    .D(WD3__Data_to_write_in_the_register_of_address_A3), .en(E31), .Q(SP),
    .clk(Clk__Detects_changes_in_the_clock), .clr(Rst__Reset_every_register_to_0));
  Multiplexer #(.select(5), .width(32), .enable("false")) multiplexer_2 (
    .in0(R0), .in1(R1), .in2(R2), .in3(R3), .in4(R4), .in5(R5), .in6(R6), .in7(R7), .in8(R8), .in9(R9),
    .in10(R10), .in11(R11), .in12(R12), .in13(R13), .in14(R14), .in15(R15), .in16(R16), .in17(R17),
    .in18(R18), .in19(R19), .in20(R20), .in21(R21), .in22(R22), .in23(R23), .in24(R24), .in25(R25),
    .in26(R26), .in27(R27), .in28(R28), .in29(R29), .in30(R30), .in31(SP),
    .out(RD2___Output__Second_data_read), .sel(A2__Address_of_the_second_register_to_read));

  // Other names for the same wires on the sheet: A1[4:0] = A1__Address_of_the_first_register_to_read;
  //   A2[4:0] = A2__Address_of_the_second_register_to_read; A3[4:0] = A3__Addres_of_the_third_register_to_write;
  //   Clk = Clk__Detects_changes_in_the_clock; RD1[31:0] = RD1___Output__First_data_read;
  //   RD2[31:0] = RD2___Output__Second_data_read; Rst = Rst__Reset_every_register_to_0;
  //   WD3[31:0] = WD3__Data_to_write_in_the_register_of_address_A3; WE3 = WE3__Enable_Disable_writing

  // Notes on the sheet:
  //   Input
  //   Registers
  //   Output
  //   Reading
  //   Writing
endmodule
